// Logisim project cpu_单级中断.circ as structural Verilog: 5 circuits, main circuit cpu
module cpu (
  output \与中断屏蔽位与 ,
  output \与中断屏蔽位与_2 ,
  output \与中断屏蔽位与_3 
);

  wire \_1号中断 , \_1号中断指示灯 , \_2号中断 , \_2号中断指示灯 , \_3号中断 , \_3号中断指示灯 , alu_1_equal, and_1_out, and_2_out,
       and_3_out, and_4_out, and_5_out, and_6_out, and_7_out, and_9_out, and_10_out, and_11_out, and_12_out,
       clk, clock_1_out, comparator_1_eq, comparator_1_lt, control_1_alu_x, control_1_en, control_1_ld_ctl,
       control_1_lw_lhu, control_1_rf_we, control_1_str_ctl, \control_1_无条件分支指令 , \control_1_有条件分支成功跳转 ,
       \control_1_有条件分支指令 , d_ff_1_q, d_ff_2_q, d_ff_3_q, Dis, eret, ext, \int , int1, int2, int3, not_1_out,
       not_2_out, not_4_out, or_4_out, or_5_out, or_6_out, or_7_out, or_8_out, or_9_out,
       priority_encoder_1_gs, rA, rB, register_1_q, RST, stall, \中断CPU ;
  wire [1:0] control_1_alu_y, control_1_npc_op, control_1_rw, priority_encoder_1_out, rfw, \当前中断信号 ;
  wire [3:0] control_1_alu_op;
  wire [4:0] decode_1_rd, decode_1_rs, decode_1_rt, multiplexer_3_out, multiplexer_4_out, registerfile_1_p6;
  wire [5:0] _5_0, _31_26;
  wire [15:0] decode_1_z_ext, incrementer_1_p2, incrementer_2_p2, incrementer_3_p2, incrementer_4_p2,
       incrementer_5_p2, multiplexer_10_out, register_5_q, \总周期数 , \无条件分支指令数 , \有条件分支成功跳转 , \有条件分支指令数 ;
  wire [23:0] mips_ram_1_p1;
  wire [25:0] decode_1_index;
  wire [31:0] adder_1_out, bit_extender_1_out, decode_1_s_ext, decode_1_shamt, epc_1_pc_out, mips_ram_1_p2,
       mips_ram_1_p7, multiplexer_1_out, multiplexer_6_out, multiplexer_7_out, multiplexer_8_out,
       multiplexer_9_out, npc_1_pc_new, PC_q, rom_1_data, SyscallOut, v0;
  wire [31:16] decode_1_z_ext_2;
  wire [31:24] alu_1_result;

  Button \u_总复位  (.out(RST));
  Button _1 (.out(\_1号中断 ));
  Button _2 (.out(\_2号中断 ));
  Button _3 (.out(\_3号中断 ));
  Hex_Digit_Display hex_digit_display_1 (.value(SyscallOut[27:24]));  // open: dp
  Hex_Digit_Display hex_digit_display_2 (.value(SyscallOut[31:28]));  // open: dp
  Hex_Digit_Display hex_digit_display_3 (.value(SyscallOut[19:16]));  // open: dp
  Hex_Digit_Display hex_digit_display_4 (.value(SyscallOut[23:20]));  // open: dp
  Clock clock_1 (.out(clock_1_out));
  or or_1 (\_1号中断指示灯 , \与中断屏蔽位与 , d_ff_1_q);
  or or_2 (\_2号中断指示灯 , \与中断屏蔽位与_2 , d_ff_2_q);
  or or_3 (\_3号中断指示灯 , \与中断屏蔽位与_3 , d_ff_3_q);
  Hex_Digit_Display hex_digit_display_5 (.value(SyscallOut[15:12]));  // open: dp
  Hex_Digit_Display hex_digit_display_6 (.value(SyscallOut[11:8]));  // open: dp
  D_Flip_Flop d_ff_1 (.clk(\_1号中断 ), .D(1'b1), .Q(d_ff_1_q), .reset(\与中断屏蔽位与 ));  // open: Qn, preset, en
  D_Flip_Flop d_ff_2 (.clk(\_2号中断 ), .D(1'b1), .Q(d_ff_2_q), .reset(\与中断屏蔽位与_2 ));  // open: Qn, preset, en
  D_Flip_Flop d_ff_3 (.clk(\_3号中断 ), .D(1'b1), .Q(d_ff_3_q), .reset(\与中断屏蔽位与_3 ));  // open: Qn, preset, en
  and and_1 (and_1_out, ~eret, \中断CPU );  // AND_Gate
  or or_4 (or_4_out, eret, \中断CPU );
  Hex_Digit_Display hex_digit_display_7 (.value(SyscallOut[7:4]));  // open: dp
  Hex_Digit_Display hex_digit_display_8 (.value(SyscallOut[3:0]));  // open: dp
  or or_5 (or_5_out, d_ff_1_q, \与中断屏蔽位与 );
  and and_2 (and_2_out, or_5_out, ~and_3_out);  // AND_Gate
  and and_3 (and_3_out, int1, eret);
  or or_6 (or_6_out, d_ff_2_q, \与中断屏蔽位与_2 );
  and and_4 (and_4_out, or_6_out, ~and_5_out);  // AND_Gate
  and and_5 (and_5_out, int2, eret);
  or or_7 (or_7_out, d_ff_3_q, \与中断屏蔽位与_3 );
  and and_6 (and_6_out, or_7_out, ~and_7_out);  // AND_Gate
  and and_7 (and_7_out, int3, eret);
  Priority_Encoder #(.select(2)) priority_encoder_1 (
    .in0(1'b0), .in1(\_1号中断指示灯 ), .in2(\_2号中断指示灯 ), .in3(\_3号中断指示灯 ), .out(priority_encoder_1_out),
    .gs(priority_encoder_1_gs));  // open: en_out, en_in
  not not_1 (not_1_out, priority_encoder_1_gs);
  or or_8 (or_8_out, \_1号中断指示灯 , \_2号中断指示灯 , \_3号中断指示灯 );
  Register #(.width(1)) register_1 (.D(and_1_out), .en(or_4_out), .Q(register_1_q), .clk(clk), .clr(RST));
  not not_2 (not_2_out, register_1_q);
  D_Flip_Flop IR1 (.clk(clock_1_out), .D(and_2_out), .Q(\与中断屏蔽位与 ), .reset(RST));  // open: Qn, preset, en
  D_Flip_Flop IR1_2 (.clk(clock_1_out), .D(and_4_out), .Q(\与中断屏蔽位与_2 ), .reset(RST));  // open: Qn, preset, en
  D_Flip_Flop IR1_3 (.clk(clock_1_out), .D(and_6_out), .Q(\与中断屏蔽位与_3 ), .reset(RST));  // open: Qn, preset, en
  Decoder #(.select(2), .enable("false")) decoder_1 (
    .out1(int1), .out2(int2), .out3(int3), .sel(\当前中断信号 ));  // open: out0
  Register #(.width(2)) register_2 (.D(priority_encoder_1_out), .en(\中断CPU ), .Q(\当前中断信号 ), .clk(clk), .clr(not_1_out));
  not not_3 (stall, or_8_out);
  and and_8 (\中断CPU , or_8_out, not_2_out);
  Register #(.width(1)) register_3 (.D(\中断CPU ), .Q(\int ), .clk(clk), .clr(RST));  // open: en
  // Probe on \总周期数 
  // Probe on \无条件分支指令数 
  // Probe on \有条件分支指令数 
  // Probe on \有条件分支成功跳转 
  // Probe on \当前中断信号 
  Clock clock_2 (.out(clk));
  LED \_1号中断等待指示灯  (.in(\_1号中断指示灯 ));
  LED \_2号中断等待指示灯  (.in(\_2号中断指示灯 ));
  LED \_3号中断等待指示灯  (.in(\_3号中断指示灯 ));
  Control control_1 (
    ._31_26(_31_26), ._5_0(_5_0), .v0(v0), .eql(alu_1_equal), ._0(or_9_out), .NPC_op(control_1_npc_op),
    .rB(rB), .display(Dis), .EN(control_1_en), .ALU_X(control_1_alu_x), .z_sh_ext(ext), .rfw(rfw),
    .ALU_Y(control_1_alu_y), .rf_we(control_1_rf_we), .ALU_op(control_1_alu_op), .rA(rA),
    .str_ctl(control_1_str_ctl), .rW(control_1_rw), .ld_ctl(control_1_ld_ctl), .lw_lhu(control_1_lw_lhu),
    .\无条件分支指令 (\control_1_无条件分支指令 ), .\有条件分支指令 (\control_1_有条件分支指令 ), .\有条件分支成功跳转 (\control_1_有条件分支成功跳转 ),
    .eret(eret));
  NPC npc_1 (
    .PC_op(control_1_npc_op), .J__rs(v0), .PC_out(PC_q), .B_offset(decode_1_z_ext),
    .JMP_index(decode_1_index), .PC_new(npc_1_pc_new));
  and and_9 (and_9_out, \control_1_无条件分支指令 , stall);
  Register #(.width(32)) PC (.D(epc_1_pc_out), .en(control_1_en), .Q(PC_q), .clk(clk), .clr(RST));
  // Incrementer incrementer_1: pin names not known; wires that end beside it: \无条件分支指令数 , incrementer_1_p2
  Register #(.width(16)) register_4 (.D(incrementer_1_p2), .en(and_9_out), .Q(\无条件分支指令数 ), .clk(clk), .clr(RST));
  Adder #(.width(32)) adder_1 (.a(PC_q), .b(32'h4), .out(adder_1_out));  // open: cin, cout
  EPC epc_1 (
    .PC_in(npc_1_pc_new), .\int (\int ), .PC_out(epc_1_pc_out), .current(\当前中断信号 ), .clk(clk), .rst(RST),
    .eret(eret));
  and and_10 (and_10_out, control_1_en, stall);
  // MIPS_RAM mips_ram_1: pin names not known; wires that end beside it: mips_ram_1_p1, mips_ram_1_p2, control_1_str_ctl, clk, control_1_ld_ctl, RST, mips_ram_1_p7
  Register #(.width(16)) register_5 (.D(incrementer_2_p2), .en(and_10_out), .Q(register_5_q), .clk(clk), .clr(RST));
  // Incrementer incrementer_2: pin names not known; wires that end beside it: register_5_q, incrementer_2_p2
  // Incrementer incrementer_3: pin names not known; wires that end beside it: register_5_q, incrementer_3_p2
  not not_4 (not_4_out, control_1_en);
  and and_11 (and_11_out, \control_1_有条件分支指令 , stall);
  Multiplexer #(.select(2), .width(32), .enable("false")) multiplexer_1 (
    .in0({alu_1_result, mips_ram_1_p1}), .in1(multiplexer_9_out), .in2(adder_1_out), .out(multiplexer_1_out),
    .sel(rfw));  // open: in3
  // Probe on rfw
  ROM #(.addrWidth(10), .dataWidth(32)) rom_1 (.addr(PC_q[11:2]), .data(rom_1_data));  // open: sel
  Multiplexer #(.width(16), .enable("false")) multiplexer_2 (
    .in0(register_5_q), .in1(incrementer_3_p2), .out(\总周期数 ), .sel(not_4_out));
  Register #(.width(16)) register_6 (.D(incrementer_4_p2), .en(and_11_out), .Q(\有条件分支指令数 ), .clk(clk), .clr(RST));
  // Incrementer incrementer_4: pin names not known; wires that end beside it: \有条件分支指令数 , incrementer_4_p2
  Multiplexer #(.width(5), .enable("false")) multiplexer_3 (
    .in0(decode_1_rs), .in1(5'b00010), .out(multiplexer_3_out), .sel(rA));
  Multiplexer #(.select(2), .width(5), .enable("false")) multiplexer_4 (
    .in0(decode_1_rd), .in1(decode_1_rt), .in2({5{1'b1}}), .out(multiplexer_4_out), .sel(control_1_rw));  // open: in3
  Decode decode_1 (
    .in_1(rom_1_data), .index(decode_1_index), .S_ext(decode_1_s_ext), ._5_0(_5_0), .rd(decode_1_rd),
    ._31_26(_31_26), .rs(decode_1_rs), .rt(decode_1_rt), .Z_ext({decode_1_z_ext_2, decode_1_z_ext}),
    .shamt(decode_1_shamt));
  // RegisterFile registerfile_1: pin names not known; wires that end beside it: multiplexer_1_out, clk, control_1_rf_we, multiplexer_4_out, multiplexer_3_out, registerfile_1_p6, v0, mips_ram_1_p2
  Multiplexer #(.width(5), .enable("false")) multiplexer_5 (
    .in0(decode_1_rt), .in1(5'b00100), .out(registerfile_1_p6), .sel(rB));
  Multiplexer #(.width(32), .enable("false")) multiplexer_6 (
    .in0({decode_1_z_ext_2, decode_1_z_ext}), .in1(decode_1_shamt), .out(multiplexer_6_out), .sel(ext));
  // Incrementer incrementer_5: pin names not known; wires that end beside it: \有条件分支成功跳转 , incrementer_5_p2
  and and_12 (and_12_out, stall, \control_1_有条件分支成功跳转 );
  Multiplexer #(.width(32), .enable("false")) multiplexer_7 (
    .in0(v0), .in1(mips_ram_1_p2), .out(multiplexer_7_out), .sel(control_1_alu_x));
  Multiplexer #(.select(2), .width(32), .enable("false")) multiplexer_8 (
    .in0(mips_ram_1_p2), .in1(decode_1_s_ext), .in2(multiplexer_6_out), .in3({32{1'b0}}),
    .out(multiplexer_8_out), .sel(control_1_alu_y));
  Register #(.width(16)) register_7 (.D(incrementer_5_p2), .en(and_12_out), .Q(\有条件分支成功跳转 ), .clk(clk), .clr(RST));
  ALU alu_1 (
    .AluOP(control_1_alu_op), .X(multiplexer_7_out), .Equal(alu_1_equal),
    .Result({alu_1_result, mips_ram_1_p1}), .Y(multiplexer_8_out));  // open: Signed_Overflow, Result_2, UnSigned_Overflow, out_9
  Multiplexer #(.width(32), .enable("false")) multiplexer_9 (
    .in0(mips_ram_1_p7), .in1(bit_extender_1_out), .out(multiplexer_9_out), .sel(control_1_lw_lhu));
  Register #(.width(32)) register_8 (.D(mips_ram_1_p2), .en(Dis), .Q(SyscallOut), .clk(clk), .clr(RST));
  Multiplexer #(.width(16), .enable("false")) multiplexer_10 (
    .in0(mips_ram_1_p7[31:16]), .in1(mips_ram_1_p7[15:0]), .out(multiplexer_10_out), .sel(mips_ram_1_p1[1]));
  assign bit_extender_1_out = {{16{multiplexer_10_out[15]}}, multiplexer_10_out};  // Bit_Extender bit_extender_1
  or or_9 (or_9_out, comparator_1_eq, comparator_1_lt);
  Comparator #(.width(32)) comparator_1 (
    .a({alu_1_result, mips_ram_1_p1}), .b({32{1'b0}}), .eq(comparator_1_eq), .lt(comparator_1_lt));  // open: gt

  // Notes on the sheet:
  //   数码管输出应该用寄存器锁存，否则显示数据只能一闪而过
  //   可以通过项目增加Logisim库的方式将前几次实验完成的电路作为子电路引入到本电路中使用
  //   数码管输出
  //   Reset 
  //   Reset 
  //   Reset 
  //   总复位信号应将除ROM以外所有存储组件全部清零
  //   contents of rom_1 (hex, n*v repeats v):
  //   20110001 8000c05 20110001 20120002 20130003 8000c09 20110001 20120002 20130003 8000c0d 20110001
  //   20120002 20130003 8000c11 20110001 20120002 20130003 c000cb8 20100001 20110001 118fc0 112020
  //   20020022 c 118882 12200001 8000c15 112020 20020022 c 20110001 118880 112020 20020022 c 12200001
  //   8000c1f 20110001 118fc0 112020 20020022 c 1188c3 112020 20020022 c 118903 112020 20020022 c 118903
  //   112020 20020022 c 118903 112020 20020022 c 118903 112020 20020022 c 118903 112020 20020022 c 118903
  //   112020 20020022 c 118903 112020 20020022 c 20100001 109fc0 139fc3 8021 2012000c 24160003 26100001
  //   3210000f 20080008 20090001 139900 2709825 132020 20020022 c 1094022 1500fff9 22100001 2018000f
  //   2188024 108700 20080008 20090001 139902 2709825 132021 20020022 c 1094022 1500fff9 108702 2c9b022
  //   12c00001 8000c50 4020 1084027 84400 3508ffff 82021 20020022 c 2010ffff 20110000 ae300000 22100001
  //   22310004 ae300000 22100001 22310004 ae300000 22100001 22310004 ae300000 22100001 22310004 ae300000
  //   22100001 22310004 ae300000 22100001 22310004 ae300000 22100001 22310004 ae300000 22100001 22310004
  //   ae300000 22100001 22310004 ae300000 22100001 22310004 ae300000 22100001 22310004 ae300000 22100001
  //   22310004 ae300000 22100001 22310004 ae300000 22100001 22310004 ae300000 22100001 22310004 ae300000
  //   22100001 22310004 22100001 8020 2011003c 8e130000 8e340000 274402a 11000002 ae330000 ae140000
  //   2231fffc 1611fff8 102020 20020022 c 22100004 2011003c 1611fff2 2002000a c 20100000 22100001 102020
  //   20020022 c 22100002 102020 20020022 c 22100003 102020 20020022 c 22100004 102020 20020022 c 22100005
  //   102020 20020022 c 22100006 102020 20020022 c 22100007 102020 20020022 c 22100008 102020 20020022
  //   20020022 c 3e00008 201d0400 23bdfffc afb00000 23bdfffc afb30000 23bdfffc afa80000 23bdfffc afa90000
  //   23bdfffc afa40000 23bdfffc afa20000 20100001 109fc0 139fc3 24100001 20080008 20090001 139900 2709825
  //   132020 20020022 c 1094022 1500fff9 8fa20000 27bd0004 8fa70000 27bd0004 8fa90000 27bd0004 8fa80000
  //   27bd0004 8fb30000 27bd0004 8fb00000 27bd0004 201d0001 42000018 201d0400 23bdfffc afb00000 23bdfffc
  //   afb30000 23bdfffc afa80000 23bdfffc afa90000 23bdfffc afa40000 23bdfffc afa20000 20100001 109fc0
  //   139fc3 24100002 20080008 20090001 139900 2709825 132020 20020022 c 1094022 1500fff9 8fa20000
  //   27bd0004 8fa70000 27bd0004 8fa90000 27bd0004 8fa80000 27bd0004 8fb30000 27bd0004 8fb00000 27bd0004
  //   201d0001 42000018 201d0400 23bdfffc afb00000 23bdfffc afb30000 23bdfffc afa80000 23bdfffc afa90000
  //   23bdfffc afa40000 23bdfffc afa20000 20100001 109fc0 139fc3 24100003 20080008 20090001 139900 2709825
  //   132020 20020022 c 1094022 1500fff9 8fa20000 27bd0004 8fa70000 27bd0004 8fa90000 27bd0004 8fa80000
  //   27bd0004 8fb30000 27bd0004 8fb00000 27bd0004 201d0001 42000018
endmodule

// CONTROL
module Control (
  input  [5:0] _31_26,
  input  [5:0] _5_0,
  input  [31:0] v0,
  input  eql,
  input  _0,
  output [1:0] NPC_op,
  output rB,
  output display,
  output EN,
  output ALU_X,
  output z_sh_ext,
  output [1:0] rfw,
  output [1:0] ALU_Y,
  output lw_lhu,
  output rf_we,
  output [3:0] ALU_op,
  output \无条件分支指令 ,
  output rA,
  output str_ctl,
  output \有条件分支指令 ,
  output [1:0] rW,
  output ld_ctl,
  output \有条件分支成功跳转 ,
  output eret
);

  wire Add, Addi, Addiu, Addu, And, and_22_out, and_23_out, and_24_out, and_25_out, and_33_out, and_34_out,
       and_35_out, and_37_out, and_38_out, and_39_out, and_40_out, Andi, Beq, Blez, Bne, comparator_1_eq,
       comparator_2_eq, comparator_3_eq, J, Jal, Jr, Lw, Nor, nor_1_out, nor_2_out, nor_3_out, nor_4_out,
       not_1_out, not_2_out, not_3_out, not_4_out, not_5_out, not_6_out, not_7_out, not_8_out, not_9_out,
       not_10_out, not_11_out, not_12_out, not_13_out, not_14_out, not_15_out, not_16_out, not_17_out,
       not_18_out, not_19_out, not_20_out, not_21_out, not_22_out, not_23_out, not_24_out, not_25_out,
       not_26_out, not_27_out, Or, or_1_out, or_2_out, or_3_out, or_4_out, or_5_out, or_6_out, or_7_out,
       or_8_out, or_9_out, or_10_out, or_17_out, or_18_out, or_20_out, or_21_out, Ori, Sll, Slt, Slti, Sltu,
       Sra, Srl, Sub, Xor, Xori;

  and and_1 (Addi, ~_31_26[5], ~_31_26[4], _31_26[3], ~_31_26[2], ~_31_26[1], ~_31_26[0]);  // AND_Gate
  and and_2 (Addiu, ~_31_26[5], ~_31_26[4], _31_26[3], ~_31_26[2], ~_31_26[1], _31_26[0]);  // AND_Gate
  and and_3 (Andi, ~_31_26[5], ~_31_26[4], _31_26[3], _31_26[2], ~_31_26[1], ~_31_26[0]);  // AND_Gate
  and and_4 (Ori, ~_31_26[5], ~_31_26[4], _31_26[3], _31_26[2], ~_31_26[1], _31_26[0]);  // AND_Gate
  and and_5 (Lw, _31_26[5], ~_31_26[4], ~_31_26[3], ~_31_26[2], _31_26[1], _31_26[0]);  // AND_Gate
  and and_6 (str_ctl, _31_26[5], ~_31_26[4], _31_26[3], ~_31_26[2], _31_26[1], _31_26[0]);  // AND_Gate
  and and_7 (Beq, ~_31_26[5], ~_31_26[4], ~_31_26[3], _31_26[2], ~_31_26[1], ~_31_26[0]);  // AND_Gate
  or or_1 (or_1_out, Add, Addu, And, Sub, Or, Xor, Nor, Beq, Bne, Slt, Sltu);
  or or_2 (or_2_out, Addi, Addiu, Lw, str_ctl, Slti, Xori, lw_lhu);
  or or_3 (or_3_out, Andi, Sll, Sra, Srl, Ori);
  or or_4 (or_4_out, Add, Addi, Addiu, Addu, Lw, str_ctl, lw_lhu);
  or or_5 (or_5_out, And, Andi);
  or or_6 (or_6_out, Sub, Blez);
  or or_7 (or_7_out, Or, Ori);
  or or_8 (or_8_out, Slt, Slti);
  or or_9 (or_9_out, Xori, Xor);
  or or_10 (or_10_out, _31_26[0], _31_26[1], _31_26[2], _31_26[3], _31_26[4], _31_26[5]);
  and and_8 (Slti, ~_31_26[5], ~_31_26[4], _31_26[3], ~_31_26[2], _31_26[1], ~_31_26[0]);  // AND_Gate
  and and_9 (J, ~_31_26[5], ~_31_26[4], ~_31_26[3], ~_31_26[2], _31_26[1], ~_31_26[0]);  // AND_Gate
  and and_10 (Jal, ~_31_26[5], ~_31_26[4], ~_31_26[3], ~_31_26[2], _31_26[1], _31_26[0]);  // AND_Gate
  and and_11 (Xori, ~_31_26[5], ~_31_26[4], _31_26[3], _31_26[2], _31_26[1], ~_31_26[0]);  // AND_Gate
  and and_12 (Bne, ~_31_26[5], ~_31_26[4], ~_31_26[3], _31_26[2], ~_31_26[1], _31_26[0]);  // AND_Gate
  and and_13 (lw_lhu, _31_26[5], ~_31_26[4], ~_31_26[3], _31_26[2], ~_31_26[1], _31_26[0]);  // AND_Gate
  and and_14 (Blez, ~_31_26[5], ~_31_26[4], ~_31_26[3], _31_26[2], _31_26[1], ~_31_26[0]);  // AND_Gate
  and and_15 (Add, ~or_10_out, _5_0[5], ~_5_0[4], ~_5_0[3], ~_5_0[2], ~_5_0[1], ~_5_0[0]);  // AND_Gate
  and and_16 (Addu, ~or_10_out, _5_0[5], ~_5_0[4], ~_5_0[3], ~_5_0[2], ~_5_0[1], _5_0[0]);  // AND_Gate
  and and_17 (And, ~or_10_out, _5_0[5], ~_5_0[4], ~_5_0[3], _5_0[2], ~_5_0[1], ~_5_0[0]);  // AND_Gate
  and and_18 (Sll, ~or_10_out, ~_5_0[5], ~_5_0[4], ~_5_0[3], ~_5_0[2], ~_5_0[1], ~_5_0[0]);  // AND_Gate
  and and_19 (Sra, ~or_10_out, ~_5_0[5], ~_5_0[4], ~_5_0[3], ~_5_0[2], _5_0[1], _5_0[0]);  // AND_Gate
  and and_20 (Srl, ~or_10_out, ~_5_0[5], ~_5_0[4], ~_5_0[3], ~_5_0[2], _5_0[1], ~_5_0[0]);  // AND_Gate
  and and_21 (Xor, ~or_10_out, _5_0[5], ~_5_0[4], ~_5_0[3], _5_0[2], _5_0[1], ~_5_0[0]);  // AND_Gate
  not not_1 (not_1_out, or_1_out);
  not not_2 (not_2_out, or_2_out);
  not not_3 (not_3_out, or_3_out);
  not not_4 (not_4_out, or_1_out);
  not not_5 (not_5_out, or_2_out);
  not not_6 (not_6_out, Blez);
  not not_7 (not_7_out, or_1_out);
  not not_8 (not_8_out, or_2_out);
  not not_9 (not_9_out, or_3_out);
  not not_10 (not_10_out, or_1_out);
  not not_11 (not_11_out, or_3_out);
  not not_12 (not_12_out, Blez);
  and and_22 (and_22_out, not_1_out, not_2_out, not_3_out, Blez);
  and and_23 (and_23_out, not_4_out, not_5_out, or_3_out, not_6_out);
  and and_24 (and_24_out, not_7_out, not_8_out, not_9_out, Blez);
  and and_25 (and_25_out, not_10_out, or_2_out, not_11_out, not_12_out);
  or or_11 (ALU_Y[1], and_22_out, and_23_out);
  or or_12 (ALU_Y[0], and_24_out, and_25_out);
  nor nor_1 (nor_1_out, Sll, Srl, or_6_out, or_7_out, Nor, Sltu);
  nor nor_2 (nor_2_out, or_4_out, Sll, Sra, or_7_out, Sltu, or_9_out);
  nor nor_3 (nor_3_out, Sll, Sra, Srl, or_7_out, Nor, or_8_out, or_9_out);
  nor nor_4 (nor_4_out, or_4_out, or_5_out, Sll, Sra, Srl, or_6_out);
  and and_26 (Sub, ~or_10_out, _5_0[5], ~_5_0[4], ~_5_0[3], ~_5_0[2], _5_0[1], ~_5_0[0]);  // AND_Gate
  and and_27 (Or, ~or_10_out, _5_0[5], ~_5_0[4], ~_5_0[3], _5_0[2], ~_5_0[1], _5_0[0]);  // AND_Gate
  and and_28 (Nor, ~or_10_out, _5_0[5], ~_5_0[4], ~_5_0[3], _5_0[2], _5_0[1], _5_0[0]);  // AND_Gate
  and and_29 (Slt, ~or_10_out, _5_0[5], ~_5_0[4], _5_0[3], ~_5_0[2], _5_0[1], ~_5_0[0]);  // AND_Gate
  and and_30 (Sltu, ~or_10_out, _5_0[5], ~_5_0[4], _5_0[3], ~_5_0[2], _5_0[1], _5_0[0]);  // AND_Gate
  and and_31 (Jr, ~or_10_out, ~_5_0[5], ~_5_0[4], _5_0[3], ~_5_0[2], ~_5_0[1], ~_5_0[0]);  // AND_Gate
  and and_32 (rA, ~or_10_out, ~_5_0[5], ~_5_0[4], _5_0[3], _5_0[2], ~_5_0[1], ~_5_0[0]);  // AND_Gate
  or or_13 (ALU_op[0], or_4_out, or_5_out, Sra, or_8_out, or_9_out, nor_1_out);
  or or_14 (ALU_op[1], or_5_out, Srl, or_6_out, Nor, or_8_out, nor_2_out);
  or or_15 (ALU_op[2], or_4_out, or_5_out, or_6_out, Sltu, nor_3_out);
  or or_16 (ALU_op[3], nor_4_out, or_7_out, Nor, or_8_out, Sltu, or_9_out);
  not not_13 (not_13_out, eql);
  or or_17 (or_17_out, J, Jal);
  and and_33 (and_33_out, Beq, eql);
  or or_18 (or_18_out, and_33_out, and_34_out, and_35_out);
  and and_34 (and_34_out, Bne, not_13_out);
  and and_35 (and_35_out, Blez, _0);
  Comparator #(.width(32)) comparator_1 (.a(v0), .b(32'ha), .eq(comparator_1_eq));  // open: gt, lt
  or or_19 (ALU_X, Sll, Sra, Srl);
  or or_20 (or_20_out, Srl, Add, Addu, And, Sll, Sra, Sub, Or, Nor, Slt, Sltu, Xor);
  or or_21 (or_21_out, Addi, Addiu, Andi, Ori, Slti, Xori, Lw, lw_lhu);
  or or_22 (ld_ctl, Lw, lw_lhu);
  nand nand_1 (EN, rA, comparator_1_eq);
  and and_36 (display, rA, ~comparator_1_eq);  // AND_Gate
  nor nor_5 (rf_we, str_ctl, Beq, Bne, J, Jr, rA, Blez);
  not not_14 (not_14_out, or_20_out);
  not not_15 (not_15_out, or_21_out);
  not not_16 (not_16_out, or_20_out);
  not not_17 (not_17_out, Jal);
  Comparator #(.width(6)) comparator_2 (.a(_31_26), .b(6'b010000), .eq(comparator_2_eq));  // open: gt, lt
  Comparator #(.width(6)) comparator_3 (.a(_5_0), .b(6'b011000), .eq(comparator_3_eq));  // open: gt, lt
  not not_18 (not_18_out, ld_ctl);
  not not_19 (not_19_out, Jal);
  not not_20 (not_20_out, or_17_out);
  not not_21 (not_21_out, or_18_out);
  and and_37 (and_37_out, not_20_out, not_21_out, Jr);
  not not_22 (not_22_out, or_17_out);
  and and_38 (and_38_out, not_22_out, or_18_out, not_23_out);
  not not_23 (not_23_out, Jr);
  not not_24 (not_24_out, or_17_out);
  not not_25 (not_25_out, or_18_out);
  and and_39 (and_39_out, not_24_out, not_25_out, Jr);
  and and_40 (and_40_out, or_17_out, not_26_out, not_27_out);
  not not_26 (not_26_out, or_18_out);
  not not_27 (not_27_out, Jr);
  and and_41 (rW[1], not_14_out, not_15_out, Jal);
  and and_42 (rW[0], not_16_out, or_21_out, not_17_out);
  and and_43 (eret, comparator_2_eq, comparator_3_eq);
  and and_44 (rfw[1], not_18_out, Jal);
  and and_45 (rfw[0], ld_ctl, not_19_out);
  or or_23 (NPC_op[1], and_37_out, and_38_out);
  or or_24 (NPC_op[0], and_39_out, and_40_out);
  nor nor_6 (z_sh_ext, Andi, Ori);
  and and_46 (\有条件分支成功跳转 , ~NPC_op[0], NPC_op[1]);  // AND_Gate
  or or_25 (\有条件分支指令 , Beq, Blez, Bne);
  or or_26 (\无条件分支指令 , J, Jal, Jr);

  assign rB = rA;

  // Other names for the same wires on the sheet: Lhu = lw_lhu; Sw = str_ctl; syscall = rA

  // Notes on the sheet:
  //   Input
  //   Output
endmodule

module NPC (
  input  [31:0] J__rs,
  input  [1:0] PC_op,
  input  [15:0] B_offset,
  input  [25:0] JMP_index,
  input  [31:0] PC_out,
  output [31:0] PC_new
);

  wire [31:0] adder_1_out, adder_2_out, bit_extender_1_out;

  Adder #(.width(32)) adder_1 (.a(adder_2_out), .b(bit_extender_1_out), .out(adder_1_out));  // open: cin, cout
  assign bit_extender_1_out = {{14{B_offset[15]}}, {B_offset, 2'b00}};  // Bit_Extender bit_extender_1
  Multiplexer #(.select(2), .width(32), .enable("false")) multiplexer_1 (
    .in0(adder_2_out), .in1({PC_out[31:28], JMP_index, 2'b00}), .in2(adder_1_out), .in3(J__rs), .out(PC_new),
    .sel(PC_op));
  Adder #(.width(32)) adder_2 (.a(32'h4), .b(PC_out), .out(adder_2_out));  // open: cin, cout
endmodule

// DECODE
module Decode (
  input  [31:0] in_1,
  output [25:0] index,
  output [31:0] S_ext,
  output [4:0] rt,
  output [31:0] Z_ext,
  output [4:0] rs,
  output [5:0] _31_26,
  output [5:0] _5_0,
  output [31:0] shamt,
  output [4:0] rd
);

  assign S_ext = {{16{in_1[15]}}, in_1[15:0]};  // Bit_Extender bit_extender_1
  assign shamt = {{27{1'b0}}, in_1[10:6]};  // Bit_Extender bit_extender_2
  assign Z_ext = {{16{1'b0}}, in_1[15:0]};  // Bit_Extender bit_extender_3

  assign _5_0 = in_1[5:0];
  assign _31_26 = in_1[31:26];
  assign index = in_1[25:0];
  assign rd = in_1[15:11];
  assign rs = in_1[25:21];
  assign rt = in_1[20:16];
endmodule

module EPC (
  input  [31:0] PC_in,
  input  \int ,
  input  eret,
  input  [1:0] current,
  input  clk,
  input  rst,
  output [31:0] PC_out
);

  wire [31:0] EPC_q, multiplexer_1_out, multiplexer_2_out;

  Multiplexer #(.select(2), .width(32), .enable("false")) multiplexer_1 (
    .in0({32{1'b0}}), .in1(32'h336c), .in2(32'h340c), .in3(32'h34ac), .out(multiplexer_1_out), .sel(current));
  Multiplexer #(.width(32), .enable("false")) multiplexer_2 (
    .in0(PC_in), .in1(multiplexer_1_out), .out(multiplexer_2_out), .sel(\int ));
  Register #(.width(32)) EPC (.D(PC_in), .en(\int ), .Q(EPC_q), .clk(clk), .clr(rst));
  Multiplexer #(.width(32), .enable("false")) multiplexer_3 (
    .in0(multiplexer_2_out), .in1(EPC_q), .out(PC_out), .sel(eret));
endmodule
