// Logisim project cpu_多级中断.circ as structural Verilog: 10 circuits, main circuit cpu
module cpu (
  output \与中断屏蔽位与 ,
  output \与中断屏蔽位与_2 ,
  output \与中断屏蔽位与_3 
);

  wire \_1号中断 , \_1号中断等待指示 , \_2号中断 , \_2号中断等待指示 , \_3号中断 , \_3号中断等待指示 , alu_1_equal, and_1_out, and_2_out,
       and_3_out, and_4_out, and_5_out, and_6_out, and_7_out, and_8_out, and_9_out, and_10_out, and_11_out,
       and_12_out, and_13_out, and_14_out, and_15_out, and_16_out, and_17_out, clk, comparator_1_eq,
       comparator_1_lt, comparator_2_gt, control_unit_1_cj, control_unit_1_data_ld, control_unit_1_display,
       control_unit_1_hlt, control_unit_1_j_success, control_unit_1_lw_ld_mul, control_unit_1_ncj,
       control_unit_1_pc_cnt, control_unit_1_str_ctl, d_ff_1_q, d_ff_2_q, d_ff_3_q, eret, int1, int2, int3,
       mfc0, mtc0, multiplexer_10_out, multiplexer_12_out, not_1_out, or_3_out, or_4_out, or_6_out, or_7_out,
       or_8_out, or_9_out, priority_encoder_1_gs, q, qwe, ra_mul, rb_mul, register_2_q, register_3_q,
       register_4_q, register_5_q, register_10_q, registerfile_1_p3, RST, test, \中断CPU ;
  wire [1:0] control_unit_1_alux_mul, control_unit_1_aluy_mul, control_unit_1_ext_ctl, current, pc_ctl,
       priority_encoder_1_out, rfw_mul, rw_mul;
  wire [3:0] control_unit_1_aluop;
  wire [4:0] decode_1_rd, decode_1_rs, decode_1_rt, decode_1_sa_hint, multiplexer_3_out, multiplexer_4_out,
       registerfile_1_p6;
  wire [5:0] decode_1_funct, decode_1_op;
  wire [15:0] decode_1_imm_offset, incrementer_1_p1, incrementer_1_p2, incrementer_2_p2, incrementer_3_p2,
       incrementer_4_p2, incrementer_5_p2, multiplexer_9_out, \总周期数 , \无条件分支指令数 , \有条件分支成功跳转 , \有条件分支指令数 ;
  wire [25:0] decode_1_addr;
  wire [31:0] AluRes, bit_extender_1_out, data, epc, mfc0_data, mips_ram_1_p7, multiplexer_1_out,
       multiplexer_2_out, multiplexer_6_out, multiplexer_7_out, num_extend_1_extend_res, pc_1_pc_out,
       registerfile_1_p7, rom_1_data, SyscallOut;

  Button \u_总复位  (.out(RST));
  pc pc_1 (
    .PC_out(pc_1_pc_out), .Offset(decode_1_imm_offset), .Jmp_addr(decode_1_addr), .clr(RST), .PC_op(pc_ctl),
    .clk(clk), .count(control_unit_1_pc_cnt), .rs_x32(registerfile_1_p7), .chooseAddr(current), .eret(eret),
    .\int (test), .epc(epc), .mtc0(mtc0), .mfc_data(mfc0_data));
  Clock clock_1 (.out(clk));
  or or_1 (\_1号中断等待指示 , \与中断屏蔽位与 , d_ff_1_q);
  Hex_Digit_Display hex_digit_display_1 (.value(SyscallOut[31:28]));  // open: dp
  Hex_Digit_Display hex_digit_display_2 (.value(SyscallOut[27:24]));  // open: dp
  D_Flip_Flop d_ff_1 (.clk(\_1号中断 ), .D(1'b1), .Q(d_ff_1_q), .reset(\与中断屏蔽位与 ));  // open: Qn, preset, en
  D_Flip_Flop d_ff_2 (.clk(\_3号中断 ), .D(1'b1), .Q(d_ff_2_q), .reset(\与中断屏蔽位与_3 ));  // open: Qn, preset, en
  or or_2 (\_3号中断等待指示 , \与中断屏蔽位与_3 , d_ff_2_q);
  Hex_Digit_Display hex_digit_display_3 (.value(SyscallOut[23:20]));  // open: dp
  Hex_Digit_Display hex_digit_display_4 (.value(SyscallOut[19:16]));  // open: dp
  or or_3 (or_3_out, d_ff_1_q, \与中断屏蔽位与 );
  and and_1 (and_1_out, int1, eret);
  or or_4 (or_4_out, d_ff_2_q, \与中断屏蔽位与_3 );
  Multiplexer #(.select(2), .width(32), .disabled(0), .enable("false")) multiplexer_1 (
    .in0(AluRes), .in1({32{1'b0}}), .in2(32'h1), .in3(data), .out(multiplexer_1_out), .sel(rfw_mul));
  Multiplexer #(.width(32), .disabled(0), .enable("false")) multiplexer_2 (
    .in0(multiplexer_1_out), .in1(mfc0_data), .out(multiplexer_2_out), .sel(mfc0));
  ROM #(.addrWidth(10), .dataWidth(32)) rom_1 (.addr(pc_1_pc_out[11:2]), .data(rom_1_data));  // open: sel
  Hex_Digit_Display hex_digit_display_5 (.value(SyscallOut[15:12]));  // open: dp
  Hex_Digit_Display hex_digit_display_6 (.value(SyscallOut[11:8]));  // open: dp
  and and_2 (and_2_out, or_3_out, ~and_1_out);  // AND_Gate
  and and_3 (and_3_out, or_4_out, ~and_4_out);  // AND_Gate
  and and_4 (and_4_out, int3, eret);
  decode decode_1 (
    .funct(decode_1_funct), .imm_offset(decode_1_imm_offset), .sa_hint(decode_1_sa_hint), .rd(decode_1_rd),
    .rt(decode_1_rt), .rs(decode_1_rs), .addr(decode_1_addr), .OP(decode_1_op), .instruction(rom_1_data));  // open: code
  Hex_Digit_Display hex_digit_display_7 (.value(SyscallOut[7:4]));  // open: dp
  Hex_Digit_Display hex_digit_display_8 (.value(SyscallOut[3:0]));  // open: dp
  D_Flip_Flop IR1 (.clk(clk), .D(and_2_out), .Q(\与中断屏蔽位与 ), .reset(RST));  // open: Qn, preset, en
  D_Flip_Flop IR3 (.clk(clk), .D(and_3_out), .Q(\与中断屏蔽位与_3 ), .reset(RST));  // open: Qn, preset, en
  Multiplexer #(.width(5), .disabled(0), .enable("false")) multiplexer_3 (
    .in0(decode_1_rs), .in1(5'b00010), .out(multiplexer_3_out), .sel(ra_mul));
  Multiplexer #(.select(2), .width(5), .disabled(0), .enable("false")) multiplexer_4 (
    .in0(decode_1_rd), .in1(decode_1_rt), .in2({5{1'b1}}), .out(multiplexer_4_out), .sel(rw_mul));  // open: in3
  // RegisterFile registerfile_1: pin names not known; wires that end beside it: multiplexer_2_out, clk, registerfile_1_p3, multiplexer_4_out, multiplexer_3_out, registerfile_1_p6, registerfile_1_p7, epc
  Multiplexer #(.width(5), .disabled(0), .enable("false")) multiplexer_5 (
    .in0(decode_1_rt), .in1(5'b00100), .out(registerfile_1_p6), .sel(rb_mul));
  num_extend num_extend_1 (
    .extend_res(num_extend_1_extend_res), .imm_offset(decode_1_imm_offset),
    .signed_unsigned_OP(control_unit_1_ext_ctl), .sa(decode_1_sa_hint));
  // Probe on \总周期数 
  // Probe on \无条件分支指令数 
  // Probe on \有条件分支指令数 
  // Probe on \有条件分支成功跳转 
  // Probe on current
  or or_5 (\_2号中断等待指示 , \与中断屏蔽位与_2 , d_ff_3_q);
  Multiplexer #(.select(2), .width(32), .disabled(0), .enable("false")) multiplexer_6 (
    .in0(registerfile_1_p7), .in1(epc), .in2(pc_1_pc_out), .out(multiplexer_6_out),
    .sel(control_unit_1_alux_mul));  // open: in3
  Multiplexer #(.select(2), .width(32), .disabled(0), .enable("false")) multiplexer_7 (
    .in0(epc), .in1(num_extend_1_extend_res), .in2(32'h4), .in3({32{1'b0}}), .out(multiplexer_7_out),
    .sel(control_unit_1_aluy_mul));
  Comparator #(.width(32)) comparator_1 (
    .a(AluRes), .b({32{1'b0}}), .eq(comparator_1_eq), .lt(comparator_1_lt));  // open: gt
  D_Flip_Flop d_ff_3 (.clk(\_2号中断 ), .D(1'b1), .Q(d_ff_3_q), .reset(\与中断屏蔽位与_2 ));  // open: Qn, preset, en
  ALU alu_1 (
    .AluOP(control_unit_1_aluop), .X(multiplexer_6_out), .Equal(alu_1_equal), .Result(AluRes),
    .Y(multiplexer_7_out));  // open: Signed_Overflow, Result_2, UnSigned_Overflow, out_9
  or or_6 (or_6_out, comparator_1_eq, comparator_1_lt);
  control_unit control_unit_1 (
    .pc_cnt(control_unit_1_pc_cnt), .pc_ctl(pc_ctl), .rfw_mul(rfw_mul), .rw_mul(rw_mul),
    .rf_we(registerfile_1_p3), .ext_ctl(control_unit_1_ext_ctl), .ra_mul(ra_mul),
    .alux_mul(control_unit_1_alux_mul), .rb_mul(rb_mul), .aluy_mul(control_unit_1_aluy_mul),
    .str_ctl(control_unit_1_str_ctl), .aluop(control_unit_1_aluop), .data_ld(control_unit_1_data_ld),
    ._31_26(decode_1_op), ._5_0(decode_1_funct), .eql(alu_1_equal), ._0_2(or_6_out),
    .lw_ld_mul(control_unit_1_lw_ld_mul), .display(control_unit_1_display), .v0(registerfile_1_p7),
    .cj(control_unit_1_cj), .j_success(control_unit_1_j_success), .ncj(control_unit_1_ncj),
    .hlt(control_unit_1_hlt), ._0(comparator_1_lt), .eret(eret), ._25_21(decode_1_rs), .mfc0(mfc0),
    .mtc0(mtc0));
  Button _1 (.out(\_1号中断 ));
  Button _2 (.out(\_2号中断 ));
  Button _3 (.out(\_3号中断 ));
  or or_7 (or_7_out, d_ff_3_q, \与中断屏蔽位与_2 );
  and and_5 (and_5_out, int2, eret);
  LED _1_2 (.in(\_1号中断等待指示 ));
  LED _2_2 (.in(\_2号中断等待指示 ));
  LED _3_2 (.in(\_3号中断等待指示 ));
  and and_6 (and_6_out, or_7_out, ~and_5_out);  // AND_Gate
  Register #(.width(32)) register_1 (.D(epc), .en(control_unit_1_display), .Q(SyscallOut), .clk(clk), .clr(RST));
  D_Flip_Flop IR2 (.clk(clk), .D(and_6_out), .Q(\与中断屏蔽位与_2 ), .reset(RST));  // open: Qn, preset, en
  Register #(.width(1)) register_2 (.D(eret), .Q(register_2_q), .clk(clk));  // open: en, clr
  // MIPS_RAM mips_ram_1: pin names not known; wires that end beside it: AluRes[25:2], epc, control_unit_1_str_ctl, clk, control_unit_1_data_ld, RST, mips_ram_1_p7
  Multiplexer #(.width(32), .disabled(0), .enable("false")) multiplexer_8 (
    .in0(mips_ram_1_p7), .in1(bit_extender_1_out), .out(data), .sel(control_unit_1_lw_ld_mul));
  Multiplexer #(.width(16), .disabled(0), .enable("false")) multiplexer_9 (
    .in0(mips_ram_1_p7[15:0]), .in1(mips_ram_1_p7[31:16]), .out(multiplexer_9_out), .sel(AluRes[1]));
  and and_7 (and_7_out, q, control_unit_1_pc_cnt);
  and and_8 (and_8_out, q, control_unit_1_cj);
  and and_9 (and_9_out, int1, register_2_q);
  and and_10 (and_10_out, int2, register_2_q);
  and and_11 (and_11_out, int3, register_2_q);
  assign bit_extender_1_out = {{16{multiplexer_9_out[15]}}, multiplexer_9_out};  // Bit_Extender bit_extender_1
  // Incrementer incrementer_1: pin names not known; wires that end beside it: incrementer_1_p1, incrementer_1_p2
  // Incrementer incrementer_2: pin names not known; wires that end beside it: \有条件分支指令数 , incrementer_2_p2
  // Incrementer incrementer_3: pin names not known; wires that end beside it: \无条件分支指令数 , incrementer_3_p2
  and and_12 (and_12_out, q, control_unit_1_ncj);
  // Incrementer incrementer_4: pin names not known; wires that end beside it: \有条件分支成功跳转 , incrementer_4_p2
  and and_13 (and_13_out, q, control_unit_1_j_success);
  Register #(.width(1)) register_3 (.D(int1), .en(int1), .Q(register_3_q), .clk(clk), .clr(and_9_out));
  Register #(.width(1)) register_4 (.D(int2), .en(int2), .Q(register_4_q), .clk(clk), .clr(and_10_out));
  Register #(.width(1)) register_5 (.D(int3), .en(int3), .Q(register_5_q), .clk(clk), .clr(and_11_out));
  Register #(.width(16)) register_6 (.D(incrementer_1_p2), .en(and_7_out), .Q(incrementer_1_p1), .clk(clk), .clr(RST));
  Register #(.width(16)) register_7 (.D(incrementer_2_p2), .en(and_8_out), .Q(\有条件分支指令数 ), .clk(clk), .clr(RST));
  Register #(.width(16)) register_8 (.D(incrementer_3_p2), .en(and_12_out), .Q(\无条件分支指令数 ), .clk(clk), .clr(RST));
  Register #(.width(16)) register_9 (.D(incrementer_4_p2), .en(and_13_out), .Q(\有条件分支成功跳转 ), .clk(clk), .clr(RST));
  Multiplexer #(.disabled(0), .enable("false")) multiplexer_10 (
    .in0(\_2号中断等待指示 ), .in1(1'b0), .out(multiplexer_10_out), .sel(qwe));
  and and_14 (and_14_out, ~mfc0, \中断CPU );  // AND_Gate
  or or_8 (or_8_out, mfc0, \中断CPU );
  Multiplexer #(.width(16), .disabled(0), .enable("false")) multiplexer_11 (
    .in0(incrementer_1_p1), .in1(incrementer_5_p2), .out(\总周期数 ), .sel(control_unit_1_hlt));
  // Incrementer incrementer_5: pin names not known; wires that end beside it: incrementer_1_p1, incrementer_5_p2
  Multiplexer #(.disabled(0), .enable("false")) multiplexer_12 (
    .in0(\_1号中断等待指示 ), .in1(1'b0), .out(multiplexer_12_out), .sel(comparator_2_gt));
  and and_15 (and_15_out, multiplexer_12_out, ~register_3_q);  // AND_Gate
  and and_16 (and_16_out, multiplexer_10_out, ~register_4_q);  // AND_Gate
  and and_17 (and_17_out, \_3号中断等待指示 , ~register_5_q);  // AND_Gate
  Register #(.width(1)) register_10 (.D(and_14_out), .en(or_8_out), .Q(register_10_q), .clk(clk), .clr(RST));
  nor nor_1 (q, int1, int2, int3);
  Priority_Encoder #(.select(2)) priority_encoder_1 (
    .in0(1'b0), .in1(\_1号中断等待指示 ), .in2(\_2号中断等待指示 ), .in3(\_3号中断等待指示 ), .out(priority_encoder_1_out),
    .gs(priority_encoder_1_gs));  // open: en_out, en_in
  Comparator #(.width(2), .mode("unsigned")) comparator_2 (
    .a(current), .b(2'b01), .gt(comparator_2_gt));  // open: eq, lt
  or or_9 (or_9_out, and_15_out, and_16_out, and_17_out);
  and and_18 (\中断CPU , or_9_out, ~register_10_q);  // AND_Gate
  Register #(.width(2)) register_11 (.D(priority_encoder_1_out), .en(1'b1), .Q(current), .clk(clk), .clr(not_1_out));
  not not_1 (not_1_out, priority_encoder_1_gs);
  Decoder #(.select(2), .enable("false")) decoder_1 (
    .out1(int1), .out2(int2), .out3(int3), .sel(current));  // open: out0
  Comparator #(.width(2), .mode("unsigned")) comparator_3 (.a(current), .b(2'b10), .gt(qwe));  // open: eq, lt
  Register #(.width(1)) register_12 (.D(\中断CPU ), .Q(test), .clk(clk), .clr(RST));  // open: en

  // Notes on the sheet:
  //   指令存储器
  //   contents of rom_1 (hex, n*v repeats v):
  //   201d0fff 20110001 8000006 20110001 20120002 20130003 800000a 20110001 20120002 20130003 800000e
  //   20110001 20120002 20130003 8000012 20110001 20120002 20130003 c0000b9 20100001 20110001 118fc0
  //   112020 20020022 c 118882 12200001 8000016 112020 20020022 c 20110001 118880 112020 20020022 c
  //   12200001 8000020 20110001 118fc0 112020 20020022 c 1188c3 112020 20020022 c 118903 112020 20020022 c
  //   118903 112020 20020022 c 118903 112020 20020022 c 118903 112020 20020022 c 118903 112020 20020022 c
  //   118903 112020 20020022 c 118903 112020 20020022 c 20100001 109fc0 139fc3 8021 2012000c 24160003
  //   26100001 3210000f 20080008 20090001 139900 2709825 132020 20020022 c 1094022 1500fff9 22100001
  //   2018000f 2188024 108700 20080008 20090001 139902 2709825 132021 20020022 c 1094022 1500fff9 108702
  //   2c9b022 12c00001 8000051 4020 1084027 84400 3508ffff 82021 20020022 c 2010ffff 20110000 ae300000
  //   22100001 22310004 ae300000 22100001 22310004 ae300000 22100001 22310004 ae300000 22100001 22310004
  //   ae300000 22100001 22310004 ae300000 22100001 22310004 ae300000 22100001 22310004 ae300000 22100001
  //   22310004 ae300000 22100001 22310004 ae300000 22100001 22310004 ae300000 22100001 22310004 ae300000
  //   22100001 22310004 ae300000 22100001 22310004 ae300000 22100001 22310004 ae300000 22100001 22310004
  //   ae300000 22100001 22310004 22100001 8020 2011003c 8e130000 8e340000 274402a 11000002 ae330000
  //   ae140000 2231fffc 1611fff8 102020 20020022 c 22100004 2011003c 1611fff2 2002000a c 20100000 22100001
  //   102020 20020022 c 22100002 102020 20020022 c 22100003 102020 20020022 c 22100004 102020 20020022 c
  //   22100005 102020 20020022 c 22100006 102020 20020022 c 22100007 102020 20020022 c 22100008 102020
  //   20020022 20020022 c 3e00008 27bdfffc afb00000 27bdfffc 40100000 afb00000 27bdfffc afb10000 27bdfffc
  //   afb20000 27bdfffc afb30000 27bdfffc afa80000 27bdfffc afa90000 27bdfffc afaa0000 27bdfffc afab0000
  //   27bdfffc afa40000 27bdfffc afa20000 20100001 109fc0 139fc3 8021 2012000c 26100001 3210000f 20080008
  //   20090001 139900 2709825 132020 20020022 c 1094022 1500fff9 8fa20000 27bd0004 8fa40000 27bd0004
  //   8fab0000 27bd0004 8faa0000 27bd0004 8fa90000 27bd0004 8fa80000 27bd0004 8fb30000 27bd0004 8fb20000
  //   27bd0004 8fb10000 27bd0004 8fb00000 40900000 27bd0004 8fb00000 27bd0004 42000018 27bdfffc afb00000
  //   27bdfffc 40100000 afb00000 27bdfffc afb10000 27bdfffc afb20000 27bdfffc afb30000 27bdfffc afa80000
  //   27bdfffc afa90000 27bdfffc afaa0000 27bdfffc afab0000 27bdfffc afa40000 27bdfffc afa20000 27bdfffc
  //   afb80000 20100001 109fc0 139fc3 8021 2012000c 26100001 3210000f 20080008 20090001 22100001 2018000f
  //   2188024 108700 20080008 20090001 139902 2709825 132021 20020022 c 1094022 1500fff9 8fb80000 27bd0004
  //   8fa20000 27bd0004 8fa40000 27bd0004 8fab0000 27bd0004 8faa0000 27bd0004 8fa90000 27bd0004 8fa80000
  //   27bd0004 8fb30000 27bd0004 8fb20000 27bd0004 8fb10000 27bd0004 8fb00000 40900000 27bd0004 8fb00000
  //   27bd0004 42000018 27bdfffc afb00000 27bdfffc 40100000 afb00000 27bdfffc afb10000 27bdfffc afb20000
  //   27bdfffc afb30000 27bdfffc afa80000 27bdfffc afa90000 27bdfffc afaa0000 27bdfffc afab0000 27bdfffc
  //   afa40000 27bdfffc afa20000 27bdfffc afb80000 20100001 109fc0 139fc3 8021 2012000c 26100001 3210000f
  //   20080008 20090001 108702 26100003 3210000f 20080008 20090001 139900 2709825 132020 20020022 c
  //   1094022 1500fff9 8fb80000 27bd0004 8fa20000 27bd0004 8fa40000 27bd0004 8fab0000 27bd0004 8faa0000
  //   27bd0004 8fa90000 27bd0004 8fa80000 27bd0004 8fb30000 27bd0004 8fb20000 27bd0004 8fb10000 27bd0004
  //   8fb00000 40900000 27bd0004 8fb00000 27bd0004 42000018
  //   Reset 
  //   数码管输出
  //   Reset 
  //   寄存器文件
  //   Reset 
  //   中断信号源及指示电路规范（优先级3>2>1>CPU(0）)
  //   数据存储器
endmodule

module pc (
  input  [15:0] Offset,
  input  [31:0] epc,
  input  [25:0] Jmp_addr,
  input  mtc0,
  input  [1:0] chooseAddr,
  input  [31:0] rs_x32,
  input  eret,
  input  [1:0] PC_op,
  input  count,
  input  \int ,
  input  clr,
  input  clk,
  output [31:0] PC_out,
  output [31:0] mfc_data
);

  wire or_1_out;
  wire [31:0] adder_1_out, adder_2_out, bit_extender_1_out, multiplexer_1_out, multiplexer_2_out,
       multiplexer_3_out, multiplexer_4_out, multiplexer_5_out;

  Adder #(.width(32)) adder_1 (.a(adder_2_out), .b(bit_extender_1_out), .out(adder_1_out));  // open: cin, cout
  assign bit_extender_1_out = {{14{Offset[15]}}, {Offset, 2'b00}};  // Bit_Extender bit_extender_1
  Multiplexer #(.select(2), .width(32), .enable("false")) multiplexer_1 (
    .in0(adder_2_out), .in1({PC_out[31:28], Jmp_addr, 2'b00}), .in2(adder_1_out), .in3(rs_x32),
    .out(multiplexer_1_out), .sel(PC_op));
  Multiplexer #(.select(2), .width(32), .enable("false")) multiplexer_2 (
    .in0({32{1'b0}}), .in1(32'h370), .in2(32'h46c), .in3(32'h590), .out(multiplexer_2_out), .sel(chooseAddr));
  Multiplexer #(.width(32), .enable("false")) multiplexer_3 (
    .in0(multiplexer_1_out), .in1(epc), .out(multiplexer_3_out), .sel(mtc0));
  Multiplexer #(.width(32), .enable("false")) multiplexer_4 (
    .in0(multiplexer_1_out), .in1(multiplexer_2_out), .out(multiplexer_4_out), .sel(\int ));
  Register #(.width(32)) u_EPC (.D(multiplexer_3_out), .en(or_1_out), .Q(mfc_data), .clk(clk), .clr(clr));
  or or_1 (or_1_out, \int , mtc0);
  Multiplexer #(.width(32), .enable("false")) multiplexer_5 (
    .in0(multiplexer_4_out), .in1(mfc_data), .out(multiplexer_5_out), .sel(eret));
  Register #(.width(32)) reg_x32 (.D(multiplexer_5_out), .en(count), .Q(PC_out), .clk(clk), .clr(clr));
  // Probe on PC_out
  Adder #(.width(32)) adder_2 (.a(32'h4), .b(PC_out), .out(adder_2_out));  // open: cin, cout

  // Other names for the same wires on the sheet: Offset_x16[15:0] = Offset; Jmp_addr_x26[25:0] = Jmp_addr;
  //   choose[1:0] = chooseAddr; clear_x1 = clr; clk_x1 = clk; PC_op_x2[1:0] = PC_op; PC_out_x32[31:0] = PC_out;
  //   stop_x1 = count

  // Notes on the sheet:
  //   Input
  //   Output
endmodule

module decode (
  input  [31:0] instruction,
  output [5:0] funct,
  output [15:0] imm_offset,
  output [4:0] sa_hint,
  output [4:0] rd,
  output [19:0] code,
  output [4:0] rt,
  output [4:0] rs,
  output [25:0] addr,
  output [5:0] OP
);


  assign addr = instruction[25:0];
  assign code = instruction[25:6];
  assign funct = instruction[5:0];
  assign imm_offset = instruction[15:0];
  assign OP = instruction[31:26];
  assign rd = instruction[15:11];
  assign rs = instruction[25:21];
  assign rt = instruction[20:16];
  assign sa_hint = instruction[10:6];

  // Other names for the same wires on the sheet: addr_x26[25:0] = instruction[25:0]; funct_x6[5:0] = instruction[5:0];
  //   imm_offset_x16[15:0] = instruction[15:0]; instruction_x32[31:0] = instruction;
  //   code_x20[19:0] = instruction[25:6]; shamt_hint_x5[4:0] = instruction[10:6]; rd_x5[4:0] = instruction[15:11];
  //   rt_x5[4:0] = instruction[20:16]; rs_base_x5[4:0] = instruction[25:21]; OP_x6[5:0] = instruction[31:26]

  // Notes on the sheet:
  //   Input
  //   Output
endmodule

module control_unit (
  input  [5:0] _31_26,
  input  [5:0] _5_0,
  input  _0,
  input  eql,
  input  _0_2,
  input  [4:0] _25_21,
  input  [31:0] v0,
  output hlt,
  output pc_cnt,
  output [1:0] pc_ctl,
  output [1:0] rfw_mul,
  output [1:0] rw_mul,
  output rf_we,
  output [1:0] ext_ctl,
  output ra_mul,
  output [1:0] alux_mul,
  output rb_mul,
  output [1:0] aluy_mul,
  output str_ctl,
  output [3:0] aluop,
  output lw_ld_mul,
  output data_ld,
  output display,
  output ncj,
  output j_success,
  output cj,
  output eret,
  output mfc0,
  output mtc0
);

  wire Add, Addi, Addiu, Addu, And, and_9_out, and_10_out, and_11_out, and_25_out, and_26_out, and_27_out,
       and_28_out, and_46_out, and_47_out, and_48_out, and_49_out, and_51_out, and_52_out, and_53_out,
       and_54_out, and_55_out, and_56_out, Andi, Beq, Blez, Bne, comparator_1_eq, comparator_2_eq,
       comparator_3_eq, comparator_4_eq, comparator_5_eq, J, Jal, Jr, Lw, Nor, not_1_out, not_2_out,
       not_3_out, not_4_out, not_5_out, not_6_out, not_7_out, not_8_out, not_9_out, not_10_out, not_11_out,
       not_12_out, not_13_out, not_14_out, not_15_out, not_16_out, not_17_out, not_18_out, not_19_out,
       not_20_out, not_21_out, not_22_out, not_23_out, not_24_out, not_25_out, not_26_out, not_27_out,
       not_28_out, not_29_out, not_30_out, not_31_out, not_33_out, not_34_out, not_35_out, not_36_out,
       not_37_out, not_38_out, not_39_out, not_40_out, Or, or_1_out, or_2_out, or_3_out, or_6_out, or_7_out,
       or_8_out, or_9_out, or_10_out, or_11_out, or_12_out, or_13_out, or_19_out, Ori, Sll, Slt, Slti, Sltiu,
       Sltu, Sra, Srl, Sub, Xori;
  wire [1:0] and_45_out;

  and and_1 (Addi, ~_31_26[5], ~_31_26[4], _31_26[3], ~_31_26[2], ~_31_26[1], ~_31_26[0]);  // AND_Gate
  and and_2 (Addiu, ~_31_26[5], ~_31_26[4], _31_26[3], ~_31_26[2], ~_31_26[1], _31_26[0]);  // AND_Gate
  and and_3 (Andi, ~_31_26[5], ~_31_26[4], _31_26[3], _31_26[2], ~_31_26[1], ~_31_26[0]);  // AND_Gate
  and and_4 (Ori, ~_31_26[5], ~_31_26[4], _31_26[3], _31_26[2], ~_31_26[1], _31_26[0]);  // AND_Gate
  and and_5 (Lw, _31_26[5], ~_31_26[4], ~_31_26[3], ~_31_26[2], _31_26[1], _31_26[0]);  // AND_Gate
  and and_6 (str_ctl, _31_26[5], ~_31_26[4], _31_26[3], ~_31_26[2], _31_26[1], _31_26[0]);  // AND_Gate
  and and_7 (Beq, ~_31_26[5], ~_31_26[4], ~_31_26[3], _31_26[2], ~_31_26[1], ~_31_26[0]);  // AND_Gate
  and and_8 (Bne, ~_31_26[5], ~_31_26[4], ~_31_26[3], _31_26[2], ~_31_26[1], _31_26[0]);  // AND_Gate
  not not_1 (not_1_out, eql);
  or or_1 (or_1_out, J, Jal);
  aluop_trans aluop_trans_1 (
    .add(Add), .addi(Addi), .addiu(Addiu), .addu(Addu), .lw(Lw), .sw(str_ctl), .jal(Jal), .lh(lw_ld_mul),
    .\and (And), .andi(Andi), .sll(Sll), .sra(Sra), .srl(Srl), .sub(Sub), .sltiu(Sltiu), .blez(Blez),
    .\or (Or), .ori(Ori), .\nor (Nor), .slt(Slt), .slti(Slti), .sltu(Sltu), .xori(Xori), .aluop(aluop));
  and and_9 (and_9_out, Beq, eql);
  or or_2 (or_2_out, and_9_out, and_10_out, and_11_out);
  and and_10 (and_10_out, Bne, not_1_out);
  and and_11 (and_11_out, Blez, _0_2);
  or or_3 (or_3_out, _31_26[0], _31_26[1], _31_26[2], _31_26[3], _31_26[4], _31_26[5]);
  and and_12 (Slti, ~_31_26[5], ~_31_26[4], _31_26[3], ~_31_26[2], _31_26[1], ~_31_26[0]);  // AND_Gate
  and and_13 (J, ~_31_26[5], ~_31_26[4], ~_31_26[3], ~_31_26[2], _31_26[1], ~_31_26[0]);  // AND_Gate
  and and_14 (Jal, ~_31_26[5], ~_31_26[4], ~_31_26[3], ~_31_26[2], _31_26[1], _31_26[0]);  // AND_Gate
  and and_15 (Xori, ~_31_26[5], ~_31_26[4], _31_26[3], _31_26[2], _31_26[1], ~_31_26[0]);  // AND_Gate
  and and_16 (Sltiu, ~_31_26[5], ~_31_26[4], _31_26[3], ~_31_26[2], _31_26[1], _31_26[0]);  // AND_Gate
  and and_17 (lw_ld_mul, _31_26[5], ~_31_26[4], ~_31_26[3], ~_31_26[2], ~_31_26[1], _31_26[0]);  // AND_Gate
  and and_18 (Blez, ~_31_26[5], ~_31_26[4], ~_31_26[3], _31_26[2], _31_26[1], ~_31_26[0]);  // AND_Gate
  not not_2 (not_2_out, or_1_out);
  not not_3 (not_3_out, or_2_out);
  not not_4 (not_4_out, or_1_out);
  not not_5 (not_5_out, Jr);
  not not_6 (not_6_out, or_1_out);
  not not_7 (not_7_out, or_2_out);
  not not_8 (not_8_out, or_2_out);
  not not_9 (not_9_out, Jr);
  nor nor_1 (rf_we, str_ctl, Beq, Bne, J, Jr, ra_mul, Blez);
  and and_19 (Add, ~or_3_out, _5_0[5], ~_5_0[4], ~_5_0[3], ~_5_0[2], ~_5_0[1], ~_5_0[0]);  // AND_Gate
  and and_20 (Addu, ~or_3_out, _5_0[5], ~_5_0[4], ~_5_0[3], ~_5_0[2], ~_5_0[1], _5_0[0]);  // AND_Gate
  and and_21 (And, ~or_3_out, _5_0[5], ~_5_0[4], ~_5_0[3], _5_0[2], ~_5_0[1], ~_5_0[0]);  // AND_Gate
  and and_22 (Sll, ~or_3_out, ~_5_0[5], ~_5_0[4], ~_5_0[3], ~_5_0[2], ~_5_0[1], ~_5_0[0]);  // AND_Gate
  and and_23 (Sra, ~or_3_out, ~_5_0[5], ~_5_0[4], ~_5_0[3], ~_5_0[2], _5_0[1], _5_0[0]);  // AND_Gate
  and and_24 (Srl, ~or_3_out, ~_5_0[5], ~_5_0[4], ~_5_0[3], ~_5_0[2], _5_0[1], ~_5_0[0]);  // AND_Gate
  and and_25 (and_25_out, not_2_out, not_3_out, Jr);
  and and_26 (and_26_out, not_4_out, or_2_out, not_5_out);
  and and_27 (and_27_out, not_6_out, not_7_out, Jr);
  and and_28 (and_28_out, or_1_out, not_8_out, not_9_out);
  Comparator #(.width(6)) comparator_1 (.a(_31_26), .b(6'b010000), .eq(comparator_1_eq));  // open: gt, lt
  Comparator #(.width(6)) comparator_2 (.a(6'b011000), .b(_5_0), .eq(comparator_2_eq));  // open: gt, lt
  Comparator #(.width(5)) comparator_3 (.a({5{1'b0}}), .b(_25_21), .eq(comparator_3_eq));  // open: gt, lt
  Comparator #(.width(5)) comparator_4 (.a(5'b00100), .b(_25_21), .eq(comparator_4_eq));  // open: gt, lt
  or or_4 (pc_ctl[1], and_25_out, and_26_out);
  or or_5 (pc_ctl[0], and_27_out, and_28_out);
  and and_29 (eret, comparator_1_eq, comparator_2_eq);
  and and_30 (mfc0, comparator_1_eq, comparator_3_eq);
  and and_31 (mtc0, comparator_1_eq, comparator_4_eq);
  and and_32 (Sub, ~or_3_out, _5_0[5], ~_5_0[4], ~_5_0[3], ~_5_0[2], _5_0[1], ~_5_0[0]);  // AND_Gate
  and and_33 (Or, ~or_3_out, _5_0[5], ~_5_0[4], ~_5_0[3], _5_0[2], ~_5_0[1], _5_0[0]);  // AND_Gate
  and and_34 (Nor, ~or_3_out, _5_0[5], ~_5_0[4], ~_5_0[3], _5_0[2], _5_0[1], _5_0[0]);  // AND_Gate
  and and_35 (Slt, ~or_3_out, _5_0[5], ~_5_0[4], _5_0[3], ~_5_0[2], _5_0[1], ~_5_0[0]);  // AND_Gate
  and and_36 (Sltu, ~or_3_out, _5_0[5], ~_5_0[4], _5_0[3], ~_5_0[2], _5_0[1], _5_0[0]);  // AND_Gate
  and and_37 (Jr, ~or_3_out, ~_5_0[5], ~_5_0[4], _5_0[3], ~_5_0[2], ~_5_0[1], ~_5_0[0]);  // AND_Gate
  and and_38 (ra_mul, ~or_3_out, ~_5_0[5], ~_5_0[4], _5_0[3], _5_0[2], ~_5_0[1], ~_5_0[0]);  // AND_Gate
  or or_6 (or_6_out, Add, Addu, And, Sub, Or, Nor, Beq, Bne, Slt, Sltu);
  or or_7 (or_7_out, lw_ld_mul, Xori, Slti, str_ctl, Lw, Addiu, Addi);
  or or_8 (or_8_out, Andi, Ori, Sltiu);
  or or_9 (or_9_out, Srl, Sra, Sll);
  or or_10 (or_10_out, Add, Addu, And, Sll, Sra, Srl, Sub, Or, Nor, Slt, Sltu);
  or or_11 (or_11_out, Addi, Addiu, Andi, Ori, Lw, Slti, Xori, Sltiu, lw_ld_mul);
  or or_12 (or_12_out, Sll, Sra, Srl);
  or or_13 (or_13_out, Addi, Addiu, Andi, Sll, Sra, Srl, Ori, Lw, str_ctl, Slti, Xori, Sltiu, lw_ld_mul);
  not not_10 (not_10_out, or_7_out);
  not not_11 (not_11_out, or_8_out);
  not not_12 (not_12_out, or_8_out);
  not not_13 (not_13_out, or_9_out);
  not not_14 (not_14_out, or_10_out);
  not not_15 (not_15_out, or_11_out);
  not not_16 (not_16_out, or_10_out);
  not not_17 (not_17_out, Jal);
  Comparator #(.width(32)) comparator_5 (.a(v0), .b(32'ha), .eq(comparator_5_eq));  // open: gt, lt
  and and_39 (display, ra_mul, ~comparator_5_eq);  // AND_Gate
  not not_18 (not_18_out, or_12_out);
  and and_40 (alux_mul[1], not_18_out, Jal);
  and and_41 (alux_mul[0], or_12_out, not_19_out);
  not not_19 (not_19_out, Jal);
  not not_20 (not_20_out, Blez);
  not not_21 (not_21_out, or_13_out);
  not not_22 (not_22_out, or_6_out);
  not not_23 (not_23_out, Jal);
  not not_24 (not_24_out, or_13_out);
  not not_25 (not_25_out, or_6_out);
  not not_26 (not_26_out, Blez);
  not not_27 (not_27_out, Jal);
  not not_28 (not_28_out, or_6_out);
  not not_29 (not_29_out, Jal);
  not not_30 (not_30_out, or_13_out);
  not not_31 (not_31_out, or_6_out);
  and and_42 (ext_ctl[1], not_10_out, not_11_out, or_9_out);
  and and_43 (ext_ctl[0], or_7_out, not_12_out, not_13_out);
  and and_44 (and_45_out[1], not_14_out, not_15_out, Jal);
  and and_45 (and_45_out[0], not_16_out, or_11_out, not_17_out);
  or or_14 (data_ld, Lw, lw_ld_mul);
  or or_15 (cj, Beq, Blez, Bne);
  or or_16 (ncj, J, Jal, Jr);
  not not_32 (hlt, pc_cnt);
  nand nand_1 (pc_cnt, ra_mul, comparator_5_eq);
  and and_46 (and_46_out, not_20_out, Jal, not_21_out, not_22_out);
  or or_17 (aluy_mul[1], and_46_out, and_47_out);
  and and_47 (and_47_out, Blez, not_23_out, not_24_out, not_25_out);
  and and_48 (and_48_out, not_26_out, not_27_out, or_13_out, not_28_out);
  or or_18 (aluy_mul[0], and_48_out, and_49_out);
  and and_49 (and_49_out, Blez, not_29_out, not_30_out, not_31_out);
  and and_50 (j_success, ~pc_ctl[0], pc_ctl[1]);  // AND_Gate
  Multiplexer #(.width(2), .enable("false")) multiplexer_1 (.in0(and_45_out), .in1(2'b01), .out(rw_mul), .sel(mfc0));
  and and_51 (and_51_out, Sltiu, _0);
  and and_52 (and_52_out, Sltiu, ~_0);  // AND_Gate
  or or_19 (or_19_out, Lw, lw_ld_mul);
  not not_33 (not_33_out, and_51_out);
  not not_34 (not_34_out, and_52_out);
  not not_35 (not_35_out, and_52_out);
  not not_36 (not_36_out, or_19_out);
  not not_37 (not_37_out, and_51_out);
  not not_38 (not_38_out, and_52_out);
  not not_39 (not_39_out, and_51_out);
  not not_40 (not_40_out, or_19_out);
  and and_53 (and_53_out, not_33_out, not_34_out, or_19_out);
  and and_54 (and_54_out, and_51_out, not_35_out, not_36_out);
  and and_55 (and_55_out, not_37_out, not_38_out, or_19_out);
  and and_56 (and_56_out, not_39_out, and_52_out, not_40_out);
  or or_20 (rfw_mul[1], and_53_out, and_54_out);
  or or_21 (rfw_mul[0], and_55_out, and_56_out);

  assign rb_mul = ra_mul;

  // Other names for the same wires on the sheet: _0_t = _0_2; Lh = lw_ld_mul; lw_lh_mul = lw_ld_mul; Sw = str_ctl;
  //   syscall = ra_mul

  // Notes on the sheet:
  //   Input
  //   Output
endmodule

module num_extend (
  input  [15:0] imm_offset,
  input  [1:0] signed_unsigned_OP,
  input  [4:0] sa,
  output [31:0] extend_res
);

  wire [15:0] multiplexer_1_out;

  Multiplexer #(.width(16), .disabled(0), .enable("false")) multiplexer_1 (
    .in0({16{1'b0}}), .in1({16{1'b1}}), .out(multiplexer_1_out), .sel(signed_unsigned_OP[0]));
  Multiplexer #(.width(16), .disabled(0), .enable("false")) multiplexer_2 (
    .in0({16{1'b0}}), .in1(multiplexer_1_out), .out(extend_res[31:16]), .sel(imm_offset[15]));
  Multiplexer #(.width(16), .disabled(0), .enable("false")) multiplexer_3 (
    .in0(imm_offset), .in1({{11{1'b0}}, sa}), .out(extend_res[15:0]), .sel(signed_unsigned_OP[1]));

  // Other names for the same wires on the sheet: sa_x5[4:0] = sa; extend_x32[31:0] = extend_res;
  //   imm_x16[15:0] = imm_offset; OP[1:0] = signed_unsigned_OP

  // Notes on the sheet:
  //   Input
  //   Output
endmodule

module aluop_trans (
  input  add,
  input  addi,
  input  addiu,
  input  addu,
  input  lw,
  input  sw,
  input  jal,
  input  lh,
  input  \and ,
  input  andi,
  input  sll,
  input  sra,
  input  srl,
  input  sub,
  input  sltiu,
  input  blez,
  input  \or ,
  input  ori,
  input  \nor ,
  input  slt,
  input  slti,
  input  sltu,
  input  xori,
  output [3:0] aluop
);

  wire nor_1_out, nor_2_out, nor_3_out, nor_4_out, or_1_out, or_2_out, or_3_out, or_4_out, or_5_out;

  or or_1 (or_1_out, add, addi, addiu, addu, lw, sw, jal, lh);
  or or_2 (or_2_out, \and , andi);
  or or_3 (or_3_out, sub, sltiu, blez);
  or or_4 (or_4_out, \or , ori);
  or or_5 (or_5_out, slt, slti);
  nor nor_1 (nor_1_out, sll, srl, or_3_out, or_4_out, \nor , sltu);
  nor nor_2 (nor_2_out, or_1_out, sll, sra, or_4_out, sltu, xori);
  nor nor_3 (nor_3_out, sll, sra, srl, or_4_out, \nor , or_5_out, xori);
  nor nor_4 (nor_4_out, or_1_out, or_2_out, sll, sra, srl, or_3_out);
  or or_6 (aluop[2], or_1_out, or_2_out, or_3_out, sltu, nor_3_out);
  or or_7 (aluop[0], or_1_out, or_2_out, sra, or_5_out, xori, nor_1_out);
  or or_8 (aluop[1], or_2_out, srl, or_3_out, \nor , or_5_out, nor_2_out);
  or or_9 (aluop[3], nor_4_out, or_4_out, \nor , or_5_out, sltu, xori);
endmodule

module IF_ID (
  input  [31:0] in_1,
  input  [31:0] in_2,
  output out_3,
  output out_4
);

  wire [31:1] register_1_q, register_2_q;

  Register #(.width(32)) register_1 (.D(in_1), .Q({register_1_q, out_3}));  // open: en, clk, clr
  Register #(.width(32)) register_2 (.D(in_2), .Q({register_2_q, out_4}));  // open: en, clk, clr
  // Pins of 1 and 32 bits meet at {register_2_q, out_4}
  // Pins of 1 and 32 bits meet at {register_1_q, out_3}
endmodule

module npc (
  input  [15:0] Offset,
  input  [25:0] Jmp_addr,
  input  [31:0] rs_x32,
  input  [1:0] PC_op,
  input  [31:0] PCIn,
  output [31:0] PC_out
);

  wire [31:0] adder_1_out, adder_2_out, bit_extender_1_out;

  Adder #(.width(32)) adder_1 (.a(PCIn), .b(32'h4), .out(adder_1_out));  // open: cin, cout
  Adder #(.width(32)) adder_2 (.a(adder_1_out), .b(bit_extender_1_out), .out(adder_2_out));  // open: cin, cout
  assign bit_extender_1_out = {{14{Offset[15]}}, {Offset, 2'b00}};  // Bit_Extender bit_extender_1
  Multiplexer #(.select(2), .width(32), .enable("false")) multiplexer_1 (
    .in0(adder_1_out), .in1({PCIn[31:28], Jmp_addr, 2'b00}), .in2(adder_2_out), .in3(rs_x32), .out(PC_out),
    .sel(PC_op));

  // Other names for the same wires on the sheet: Offset_x16[15:0] = Offset; Jmp_addr_x26[25:0] = Jmp_addr;
  //   PC_op_x2[1:0] = PC_op; PC_out_x32[31:0] = PC_out; PCIn_x32[31:0] = PCIn

  // Notes on the sheet:
  //   Input
  //   Output
endmodule

module \中断识别  (
  input  IR1,
  input  IR2,
  input  IR3,
  input  INM1,
  input  IE,
  input  INM2,
  input  INM3,
  output [1:0] out_8,
  output zdCtrl
);

  wire and_1_out, and_2_out, and_3_out, not_1_out, not_2_out, not_3_out, or_1_out;

  not not_1 (not_1_out, INM1);
  not not_2 (not_2_out, INM2);
  not not_3 (not_3_out, INM3);
  and and_1 (and_1_out, IR1, not_1_out);
  and and_2 (and_2_out, IR2, not_2_out);
  and and_3 (and_3_out, IR3, not_3_out);
  or or_1 (or_1_out, and_1_out, and_2_out, and_3_out);
  Priority_Encoder #(.select(2)) priority_encoder_1 (
    .in0(1'b1), .in1(and_1_out), .in2(and_2_out), .in3(and_3_out), .out(out_8));  // open: gs, en_out, en_in
  and and_4 (zdCtrl, or_1_out, IE);
endmodule

module \中断采样  (
  input  IR1,
  input  IR2,
  input  \同步清零信号 ,
  input  IR3,
  input  INM1,
  input  IR3_2,
  input  \同步清零信号_2 ,
  input  INM2,
  input  INM3,
  input  \同步清零信号_3 ,
  output \与中断屏蔽位与 ,
  output [1:0] out_12,
  output \与中断屏蔽位与_2 ,
  output zdCtrl,
  output \与中断屏蔽位与_3 
);

  wire \_1号中断_out , \_2号中断_out , \_3号中断_out , and_1_out, and_2_out, and_3_out, and_4_out, and_5_out,
       and_6_out, and_7_out, clk, d_ff_1_q, d_ff_2_q, d_ff_3_q, not_1_out, not_2_out, not_3_out, not_4_out,
       not_5_out, or_1_out, or_2_out, or_3_out, or_4_out, or_5_out, or_6_out, or_7_out, or_8_out,
       register_1_q, undriven, undriven_2, undriven_3;

  Clock clock_1 (.out(clk));
  Button \_1号中断  (.out(\_1号中断_out ));
  LED \_1号中断等待指示灯  (.in(or_1_out));
  LED \_2号中断等待指示灯  (.in(or_2_out));
  or or_1 (or_1_out, \与中断屏蔽位与 , d_ff_1_q);
  Button \_2号中断  (.out(\_2号中断_out ));
  or or_2 (or_2_out, \与中断屏蔽位与_2 , d_ff_2_q);
  Button \_3号中断  (.out(\_3号中断_out ));
  or or_3 (or_3_out, \与中断屏蔽位与_3 , d_ff_3_q);
  LED \_3号中断等待指示灯  (.in(or_3_out));
  D_Flip_Flop d_ff_1 (.clk(\_1号中断_out ), .D(1'b1), .Q(d_ff_1_q), .reset(\与中断屏蔽位与 ));  // open: Qn, preset, en
  D_Flip_Flop d_ff_2 (.clk(\_2号中断_out ), .D(1'b1), .Q(d_ff_2_q), .reset(\与中断屏蔽位与_2 ));  // open: Qn, preset, en
  D_Flip_Flop d_ff_3 (.clk(\_3号中断_out ), .D(1'b1), .Q(d_ff_3_q), .reset(\与中断屏蔽位与_3 ));  // open: Qn, preset, en
  or or_4 (or_4_out, d_ff_1_q, \与中断屏蔽位与 );
  or or_5 (or_5_out, d_ff_2_q, \与中断屏蔽位与_2 );
  or or_6 (or_6_out, d_ff_3_q, \与中断屏蔽位与_3 );
  and and_1 (and_1_out, or_4_out, ~\同步清零信号 );  // AND_Gate
  and and_2 (and_2_out, or_5_out, ~\同步清零信号_2 );  // AND_Gate
  and and_3 (and_3_out, or_6_out, ~\同步清零信号_3 );  // AND_Gate
  D_Flip_Flop u_IR1 (.clk(clk), .D(and_1_out), .Q(\与中断屏蔽位与 ));  // open: Qn, preset, en, reset
  D_Flip_Flop u_IR2 (.clk(clk), .D(and_2_out), .Q(\与中断屏蔽位与_2 ));  // open: Qn, preset, en, reset
  D_Flip_Flop u_IR3 (.clk(clk), .D(and_3_out), .Q(\与中断屏蔽位与_3 ));  // open: Qn, preset, en, reset
  not not_1 (not_1_out, INM1);
  not not_2 (not_2_out, INM2);
  not not_3 (not_3_out, INM3);
  and and_4 (and_4_out, undriven_2, not_1_out);
  and and_5 (and_5_out, undriven_3, not_2_out);
  and and_6 (and_6_out, undriven, not_3_out);
  not not_4 (not_4_out, IR3_2);
  or or_7 (or_7_out, IR3_2, zdCtrl);
  Register #(.width(1)) register_1 (.D(and_7_out), .en(or_7_out), .Q(register_1_q), .clk(clk));  // open: clr
  and and_7 (and_7_out, not_4_out, zdCtrl);
  or or_8 (or_8_out, and_4_out, and_5_out, and_6_out);
  not not_5 (not_5_out, register_1_q);
  Priority_Encoder #(.select(2)) priority_encoder_1 (
    .in0(1'b1), .in1(and_4_out), .in2(and_5_out), .in3(and_6_out), .out(out_12));  // open: gs, en_out, en_in
  and and_8 (zdCtrl, or_8_out, not_5_out);

  // Notes on the sheet:
  //   Reset 
  //   Reset 
  //   Reset 
endmodule
