// Logisim project cpu_气泡.circ as structural Verilog: 12 circuits, main circuit cpu
module cpu (
);

  wire alu_1_equal, and_1_out, clock_1_out, Cond, Condit, Condit_Sec, control_1_alu_x, control_1_display,
       control_1_en, control_1_ld_ctl, control_1_lw_lhu, control_1_ra, control_1_rb, control_1_rf_we,
       control_1_str_ctl, control_1_z_sh_ext, EN_MEM, \ex_mem流水_1_en_mem , \ex_mem流水_1_ld_ctl_mem ,
       \ex_mem流水_1_lw_lhu_mem , \ex_mem流水_1_str_ctl_mem , \id_ex流水_1_display_ex , \id_ex流水_1_en_ex ,
       \id_ex流水_1_ld_ctl_ex , \id_ex流水_1_lw_lhu_ex , \id_ex流水_1_str_ctl_ex , Jump, not_1_out, not_2_out,
       or_1_out, rA, rB, register_2_q, rf_we, rf_we_EX, rf_we_MEM, RST, stall, Uncond;
  wire [1:0] control_1_alu_y, control_1_rfw, control_1_rw_ctl, \ex_mem流水_1_rfw_mem , \id_ex流水_1_rfw_ex ,
       NPC_op;
  wire [3:0] control_1_alu_op, \id_ex流水_1_alu_op_ex ;
  wire [4:0] decode_1_rd, decode_1_rs, decode_1_rt, regfile_1_ra, regfile_1_rb, regfile_1_rw_out, rW, rW_EX,
       rW_MEM;
  wire [5:0] control_1_jump_id, decode_1__5_0, decode_1__31_26, \id_ex流水_1_jump_ex ;
  wire [15:0] \总周期数 , \数据冲突数 , \无条件分支指令数 , \有条件分支成功跳转 , \有条件分支指令数 ;
  wire [25:0] index, index_EX;
  wire [31:0] alu_1_result, control_1_pcout, \ex_mem流水_1_pc_mem , \ex_mem流水_1_rb_mem ,
       \ex_mem流水_1_result_mem , \id_ex流水_1_alu_y_ex , \id_ex流水_1_rb_ex , \if_id流水_1_idin ,
       \if_id流水_1_pc_4_id , \mem_wb流水_1_w_mem , mips_ram_1_p6, npc_1_pc_new, pc_1_pc_now, PC_EX, regfile_1_b,
       rom_1_data, S_ext, shamt, SyscallOut, v0, v0_EX, Z_ext, Z_ext_EX;

  Button \u_总复位  (.out(RST));
  not not_1 (not_1_out, stall);
  Clock clock_1 (.out(clock_1_out));
  PC pc_1 (.EN(and_1_out), .clk(clock_1_out), .PC_now(pc_1_pc_now), .rst(RST), .PC_new(npc_1_pc_new));
  and and_1 (and_1_out, not_1_out, not_2_out);
  Hex_Digit_Display hex_digit_display_1 (.value(SyscallOut[27:24]));  // open: dp
  Hex_Digit_Display hex_digit_display_2 (.value(SyscallOut[31:28]));  // open: dp
  // Probe on pc_1_pc_now[11:2]
  NPC npc_1 (
    .J__rs(v0_EX), .B_offset(Z_ext_EX[15:0]), .JMP_index(index_EX), .PC_new(npc_1_pc_new), .NPC_op(NPC_op),
    .PC_in(pc_1_pc_now), .\PC_有条件 (PC_EX), .PC_Con(Cond));
  Hex_Digit_Display hex_digit_display_3 (.value(SyscallOut[23:20]));  // open: dp
  Hex_Digit_Display hex_digit_display_4 (.value(SyscallOut[19:16]));  // open: dp
  Hex_Digit_Display hex_digit_display_5 (.value(SyscallOut[15:12]));  // open: dp
  Hex_Digit_Display hex_digit_display_6 (.value(SyscallOut[11:8]));  // open: dp
  // Probe on \if_id流水_1_idin 
  \IF_ID流水  \if_id流水_1  (
    .IFin(rom_1_data), .clk(clock_1_out), .PC_4_IF(pc_1_pc_now), .IDin(\if_id流水_1_idin ),
    .PC_4_ID(\if_id流水_1_pc_4_id ), .RST(RST), .Jump(Jump), .conflict(stall));
  ROM #(.addrWidth(10), .dataWidth(32)) rom_1 (.addr(pc_1_pc_now[11:2]), .data(rom_1_data));  // open: sel
  Hex_Digit_Display hex_digit_display_7 (.value(SyscallOut[7:4]));  // open: dp
  Hex_Digit_Display hex_digit_display_8 (.value(SyscallOut[3:0]));  // open: dp
  Decode decode_1 (
    .in_1(\if_id流水_1_idin ), .index(index), .S_ext(S_ext), .Z_ext(Z_ext), ._5_0(decode_1__5_0),
    ._31_26(decode_1__31_26), .rs(decode_1_rs), .rt(decode_1_rt), .rd(decode_1_rd), .shamt_ext(shamt));
  Control control_1 (
    ._31_26(decode_1__31_26), ._5_0(decode_1__5_0), .v0(v0), .rB(control_1_rb), .EN(control_1_en),
    .ALU_X(control_1_alu_x), .ALU_Y(control_1_alu_y), .rf_we(control_1_rf_we), .ALU_op(control_1_alu_op),
    .rA(control_1_ra), .str_ctl(control_1_str_ctl), .rW_ctl(control_1_rw_ctl), .display(control_1_display),
    .ld_ctl(control_1_ld_ctl), .rfw(control_1_rfw), .Jump_ID(control_1_jump_id), .lw_lhu(control_1_lw_lhu),
    .PCin(\if_id流水_1_pc_4_id ), .PCout(control_1_pcout), .z_sh_ext(control_1_z_sh_ext), .rA_on(rA), .rB_on(rB));
  Counter #(.width(16), .max('hffff)) counter_1 (
    .count(stall), .Q(\数据冲突数 ), .clk(clock_1_out), .clr(RST));  // open: load, D, carry
  // Probe on \总周期数 
  // Probe on \无条件分支指令数 
  // Probe on \有条件分支指令数 
  // Probe on \有条件分支成功跳转 
  // Probe on \数据冲突数 
  Regfile regfile_1 (
    .W(\mem_wb流水_1_w_mem ), .clk(clock_1_out), .rf_we(rf_we), .rA_ctl(control_1_ra), .rs(decode_1_rs),
    .rB_ctl(control_1_rb), .rt(decode_1_rt), .A(v0), .B(regfile_1_b), .rA(regfile_1_ra), .rB(regfile_1_rb),
    .rd(decode_1_rd), .rW_ctl(control_1_rw_ctl), .rW_out(regfile_1_rw_out), .rW(rW), .ALU_X(control_1_alu_x));
  Data_Conflict data_conflict_1 (
    .rW_EX(rW_EX), .rA(regfile_1_ra), .rW_MEM(rW_MEM), .rB(regfile_1_rb), .rf_we_EX(rf_we_EX),
    .rf_we_MEM(rf_we_MEM), .J(Jump), .rA_on(rA), .rB_on(rB), .stall(stall));
  or or_1 (or_1_out, stall, Jump);
  \ID_EX流水  \id_ex流水_1  (
    .S_ext_ID(S_ext), .clk(clock_1_out), .RA_ID(v0), .rf_we_ID(control_1_rf_we), .RB_ID(regfile_1_b),
    .ALU_op_ID(control_1_alu_op), .str_ctl_ID(control_1_str_ctl), .EN_ID(control_1_en), .RA_EX(v0_EX),
    .rf_we_EX(rf_we_EX), .RB_EX(\id_ex流水_1_rb_ex ), .ALU_op_EX(\id_ex流水_1_alu_op_ex ),
    .str_ctl_EX(\id_ex流水_1_str_ctl_ex ), .EN_EX(\id_ex流水_1_en_ex ), .rst(RST), .ALU_Y_ID(control_1_alu_y),
    .Z_ext_ID(Z_ext), .rW_ID(regfile_1_rw_out), .rW_EX(rW_EX), .ALU_Y_EX(\id_ex流水_1_alu_y_ex ),
    .display_ID(control_1_display), .display_EX(\id_ex流水_1_display_ex ), .stall(or_1_out),
    .Jump_EX(\id_ex流水_1_jump_ex ), .Jump_ID(control_1_jump_id), .Z_ext_EX(Z_ext_EX), .index_ID(index),
    .index_EX(index_EX), .rfw_ID(control_1_rfw), .rfw_EX(\id_ex流水_1_rfw_ex ), .ld_ctl_ID(control_1_ld_ctl),
    .ld_ctl_EX(\id_ex流水_1_ld_ctl_ex ), .lw_lhu_ID(control_1_lw_lhu), .lw_lhu_EX(\id_ex流水_1_lw_lhu_ex ),
    .PC_ID(control_1_pcout), .PC_EX(PC_EX), .ext_ID(control_1_z_sh_ext), .Shamt_ID(shamt));
  // Probe on S_ext
  Counter #(.width(16), .max('hffff)) counter_2 (
    .count(Condit), .Q(\有条件分支指令数 ), .clk(clock_1_out), .clr(RST));  // open: load, D, carry
  // Probe on v0_EX
  // Probe on \id_ex流水_1_alu_y_ex 
  Register #(.width(32)) register_1 (
    .D(\id_ex流水_1_rb_ex ), .en(\id_ex流水_1_display_ex ), .Q(SyscallOut), .clk(clock_1_out), .clr(RST));
  ALU alu_1 (
    .AluOP(\id_ex流水_1_alu_op_ex ), .X(v0_EX), .Equal(alu_1_equal), .Result(alu_1_result),
    .Y(\id_ex流水_1_alu_y_ex ));  // open: Signed_Overflow, Result_2, UnSigned_Overflow, out_9
  Ctl_Conflict ctl_conflict_1 (
    .NPC_op(NPC_op), .Result(alu_1_result), .eql(alu_1_equal), .Jump_EX(\id_ex流水_1_jump_ex ), .Con(Cond),
    .Uncondit(Uncond), .Condit_Sec(Condit_Sec), .Jump(Jump), .Condit(Condit));
  Counter #(.width(16), .max('hffff)) counter_3 (
    .count(Uncond), .Q(\无条件分支指令数 ), .clk(clock_1_out), .clr(RST));  // open: load, D, carry
  \EX_MEM流水  \ex_mem流水_1  (
    .Result_EX(alu_1_result), .rW_EX(rW_EX), .Result_MEM(\ex_mem流水_1_result_mem ), .rst(RST),
    .rW_MEM(rW_MEM), .clk(clock_1_out), .str_ctl_EX(\id_ex流水_1_str_ctl_ex ),
    .str_ctl_MEM(\ex_mem流水_1_str_ctl_mem ), .EN_EX(\id_ex流水_1_en_ex ), .EN_MEM(\ex_mem流水_1_en_mem ),
    .RB_EX(\id_ex流水_1_rb_ex ), .RB_MEM(\ex_mem流水_1_rb_mem ), .rf_we_EX(rf_we_EX), .rf_we_MEM(rf_we_MEM),
    .ld_ctl_EX(\id_ex流水_1_ld_ctl_ex ), .ld_ctl_MEM(\ex_mem流水_1_ld_ctl_mem ), .rfw_EX(\id_ex流水_1_rfw_ex ),
    .rfw_MEM(\ex_mem流水_1_rfw_mem ), .lw_lhu_EX(\id_ex流水_1_lw_lhu_ex ), .lw_lhu_MEM(\ex_mem流水_1_lw_lhu_mem ),
    .PC_EX(PC_EX), .PC_MEM(\ex_mem流水_1_pc_mem ));
  // MIPS_RAM mips_ram_1: pin names not known; wires that end beside it: \ex_mem流水_1_rb_mem , \ex_mem流水_1_str_ctl_mem , clock_1_out, \ex_mem流水_1_ld_ctl_mem , RST, mips_ram_1_p6
  \MEM_WB流水  \mem_wb流水_1  (
    .Result_MEM(\ex_mem流水_1_result_mem ), .clk(clock_1_out), .rW_MEM(rW_MEM), .EN_MEM(\ex_mem流水_1_en_mem ),
    .rst(RST), .rW_WB(rW), .EN_WB(EN_MEM), .rf_we_MEM(rf_we_MEM), .rf_we_WB(rf_we),
    .MemData_MEM(mips_ram_1_p6), .PC_MEM(\ex_mem流水_1_pc_mem ), .W_MEM(\mem_wb流水_1_w_mem ),
    .lw_lhu_MEM(\ex_mem流水_1_lw_lhu_mem ), .rfw_MEM(\ex_mem流水_1_rfw_mem ));
  Counter #(.width(16), .max('hffff)) counter_4 (
    .count(Condit_Sec), .Q(\有条件分支成功跳转 ), .clk(clock_1_out), .clr(RST));  // open: load, D, carry
  Register #(.width(1)) register_2 (.D(EN_MEM), .en(EN_MEM), .Q(register_2_q), .clk(clock_1_out), .clr(RST));
  not not_2 (not_2_out, register_2_q);
  Counter #(.width(16), .max('hffff)) counter_5 (
    .load(1'b0), .count(not_2_out), .Q(\总周期数 ), .clk(clock_1_out), .clr(RST));  // open: D, carry
  // Probe on \总周期数 

  // Notes on the sheet:
  //   数码管输出应该用寄存器锁存，否则显示数据只能一闪而过
  //   可以通过项目增加Logisim库的方式将前几次实验完成的电路作为子电路引入到本电路中使用
  //   指令存储器
  //   contents of rom_1 (hex, n*v repeats v):
  //   20110001 8000c05 20110001 20120002 20130003 8000c09 20110001 20120002 20130003 8000c0d 20110001
  //   20120002 20130003 8000c11 20110001 20120002 20130003 c000cb8 20100001 20110001 118fc0 112020
  //   20020022 c 118882 12200001 8000c15 112020 20020022 c 20110001 118880 112020 20020022 c 12200001
  //   8000c1f 20110001 118fc0 112020 20020022 c 1188c3 112020 20020022 c 118903 112020 20020022 c 118903
  //   112020 20020022 c 118903 112020 20020022 c 118903 112020 20020022 c 118903 112020 20020022 c 118903
  //   112020 20020022 c 118903 112020 20020022 c 20100001 109fc0 139fc3 8021 2012000c 24160003 26100001
  //   3210000f 20080008 20090001 139900 2709825 132020 20020022 c 1094022 1500fff9 22100001 2018000f
  //   2188024 108700 20080008 20090001 139902 2709825 132021 20020022 c 1094022 1500fff9 108702 2c9b022
  //   12c00001 8000c50 4020 1084027 84400 3508ffff 82021 20020022 c 2010ffff 20110000 ae300000 22100001
  //   22310004 ae300000 22100001 22310004 ae300000 22100001 22310004 ae300000 22100001 22310004 ae300000
  //   22100001 22310004 ae300000 22100001 22310004 ae300000 22100001 22310004 ae300000 22100001 22310004
  //   ae300000 22100001 22310004 ae300000 22100001 22310004 ae300000 22100001 22310004 ae300000 22100001
  //   22310004 ae300000 22100001 22310004 ae300000 22100001 22310004 ae300000 22100001 22310004 ae300000
  //   22100001 22310004 22100001 8020 2011003c 8e130000 8e340000 274402a 11000002 ae330000 ae140000
  //   2231fffc 1611fff8 102020 20020022 c 22100004 2011003c 1611fff2 2002000a c 20100000 22100001 102020
  //   20020022 c 22100002 102020 20020022 c 22100003 102020 20020022 c 22100004 102020 20020022 c 22100005
  //   102020 20020022 c 22100006 102020 20020022 c 22100007 102020 20020022 c 22100008 102020 20020022
  //   20020022 c 3e00008
  //   数码管输出
  //   总复位信号应将除ROM以外所有存储组件全部清零
endmodule

// IF/ID
module \IF_ID流水  (
  input  conflict,
  input  [31:0] IFin,
  input  clk,
  input  [31:0] PC_4_IF,
  input  RST,
  input  Jump,
  output [31:0] IDin,
  output [31:0] PC_4_ID
);

  wire not_1_out;
  wire [31:0] multiplexer_1_out, multiplexer_2_out;

  Multiplexer #(.width(32), .enable("false")) multiplexer_1 (
    .in0(IFin), .in1({32{1'b0}}), .out(multiplexer_1_out), .sel(Jump));
  Multiplexer #(.width(32), .enable("false")) multiplexer_2 (
    .in0(PC_4_IF), .in1({32{1'b0}}), .out(multiplexer_2_out), .sel(Jump));
  not not_1 (not_1_out, conflict);
  Register #(.width(32)) register_1 (.D(multiplexer_1_out), .en(not_1_out), .Q(IDin), .clk(clk), .clr(RST));
  Register #(.width(32)) register_2 (.D(multiplexer_2_out), .en(not_1_out), .Q(PC_4_ID), .clk(clk), .clr(RST));
endmodule

// ID/EX
module \ID_EX流水  (
  input  [31:0] S_ext_ID,
  input  [1:0] ALU_Y_ID,
  input  clk,
  input  rst,
  input  [1:0] rfw_ID,
  input  [31:0] RA_ID,
  input  [5:0] Jump_ID,
  input  rf_we_ID,
  input  [31:0] RB_ID,
  input  display_ID,
  input  [31:0] Z_ext_ID,
  input  ld_ctl_ID,
  input  lw_lhu_ID,
  input  [3:0] ALU_op_ID,
  input  str_ctl_ID,
  input  ext_ID,
  input  [4:0] rW_ID,
  input  [31:0] Shamt_ID,
  input  EN_ID,
  input  [25:0] index_ID,
  input  [31:0] PC_ID,
  input  stall,
  output [31:0] RB_EX,
  output [1:0] rfw_EX,
  output [31:0] RA_EX,
  output [5:0] Jump_EX,
  output [31:0] ALU_Y_EX,
  output rf_we_EX,
  output display_EX,
  output [31:0] Z_ext_EX,
  output ld_ctl_EX,
  output lw_lhu_EX,
  output [3:0] ALU_op_EX,
  output str_ctl_EX,
  output [4:0] rW_EX,
  output EN_EX,
  output [25:0] index_EX,
  output [31:0] PC_EX
);

  wire ext_EX, multiplexer_6_out, multiplexer_13_out, multiplexer_14_out, multiplexer_15_out,
       multiplexer_16_out, multiplexer_17_out, not_1_out;
  wire [1:0] ALU_Y_EX_t, multiplexer_10_out, multiplexer_11_out;
  wire [3:0] multiplexer_5_out;
  wire [4:0] multiplexer_7_out;
  wire [5:0] multiplexer_12_out;
  wire [25:0] multiplexer_8_out;
  wire [31:0] multiplexer_1_out, multiplexer_2_out, multiplexer_3_out, multiplexer_4_out, multiplexer_9_out,
       multiplexer_18_out, multiplexer_19_out, S_ext_EX, Shamt_EX;

  not not_1 (not_1_out, EN_ID);
  // Probe on PC_ID
  Multiplexer #(.width(32), .enable("false")) multiplexer_1 (
    .in0(S_ext_ID), .in1({32{1'b0}}), .out(multiplexer_1_out), .sel(stall));
  Multiplexer #(.width(32), .enable("false")) multiplexer_2 (
    .in0(RA_ID), .in1({32{1'b0}}), .out(multiplexer_2_out), .sel(stall));
  Multiplexer #(.width(32), .enable("false")) multiplexer_3 (
    .in0(RB_ID), .in1({32{1'b0}}), .out(multiplexer_3_out), .sel(stall));
  Multiplexer #(.width(32), .enable("false")) multiplexer_4 (
    .in0(Z_ext_ID), .in1({32{1'b0}}), .out(multiplexer_4_out), .sel(stall));
  Multiplexer #(.width(4), .enable("false")) multiplexer_5 (
    .in0(ALU_op_ID), .in1(4'b0000), .out(multiplexer_5_out), .sel(stall));
  Multiplexer #(.enable("false")) multiplexer_6 (.in0(str_ctl_ID), .in1(1'b0), .out(multiplexer_6_out), .sel(stall));
  Multiplexer #(.width(5), .enable("false")) multiplexer_7 (
    .in0(rW_ID), .in1({5{1'b0}}), .out(multiplexer_7_out), .sel(stall));
  Multiplexer #(.width(26), .enable("false")) multiplexer_8 (
    .in0(index_ID), .in1({26{1'b0}}), .out(multiplexer_8_out), .sel(stall));
  Multiplexer #(.width(32), .enable("false")) multiplexer_9 (
    .in0(PC_ID), .in1({32{1'b0}}), .out(multiplexer_9_out), .sel(stall));
  Register #(.width(32)) register_1 (.D(multiplexer_1_out), .en(1'b1), .Q(S_ext_EX), .clk(clk), .clr(rst));
  Register #(.width(32)) register_2 (.D(multiplexer_2_out), .en(1'b1), .Q(RA_EX), .clk(clk), .clr(rst));
  Register #(.width(32)) register_3 (.D(multiplexer_3_out), .en(1'b1), .Q(RB_EX), .clk(clk), .clr(rst));
  Register #(.width(32)) register_4 (.D(multiplexer_4_out), .en(1'b1), .Q(Z_ext_EX), .clk(clk), .clr(rst));
  Register #(.width(4)) register_5 (.D(multiplexer_5_out), .en(1'b1), .Q(ALU_op_EX), .clk(clk), .clr(rst));
  Register #(.width(1)) register_6 (.D(multiplexer_6_out), .en(1'b1), .Q(str_ctl_EX), .clk(clk), .clr(rst));
  Register #(.width(5)) register_7 (.D(multiplexer_7_out), .en(1'b1), .Q(rW_EX), .clk(clk), .clr(rst));
  Register #(.width(1)) register_8 (.D(not_1_out), .en(1'b1), .Q(EN_EX), .clk(clk), .clr(rst));
  Register #(.width(26)) register_9 (.D(multiplexer_8_out), .en(1'b1), .Q(index_EX), .clk(clk), .clr(rst));
  Register #(.width(32)) register_10 (.D(multiplexer_9_out), .en(1'b1), .Q(PC_EX), .clk(clk), .clr(rst));
  // Probe on PC_EX
  Multiplexer #(.width(2), .enable("false")) multiplexer_10 (
    .in0(ALU_Y_ID), .in1(2'b00), .out(multiplexer_10_out), .sel(stall));
  Multiplexer #(.width(2), .enable("false")) multiplexer_11 (
    .in0(rfw_ID), .in1(2'b00), .out(multiplexer_11_out), .sel(stall));
  Multiplexer #(.width(6), .enable("false")) multiplexer_12 (
    .in0(Jump_ID), .in1({6{1'b0}}), .out(multiplexer_12_out), .sel(stall));
  Multiplexer #(.enable("false")) multiplexer_13 (.in0(rf_we_ID), .in1(1'b0), .out(multiplexer_13_out), .sel(stall));
  Multiplexer #(.enable("false")) multiplexer_14 (.in0(display_ID), .in1(1'b0), .out(multiplexer_14_out), .sel(stall));
  Multiplexer #(.enable("false")) multiplexer_15 (.in0(ld_ctl_ID), .in1(1'b0), .out(multiplexer_15_out), .sel(stall));
  Multiplexer #(.enable("false")) multiplexer_16 (.in0(lw_lhu_ID), .in1(1'b0), .out(multiplexer_16_out), .sel(stall));
  Multiplexer #(.enable("false")) multiplexer_17 (.in0(ext_ID), .in1(1'b0), .out(multiplexer_17_out), .sel(stall));
  Multiplexer #(.width(32), .enable("false")) multiplexer_18 (
    .in0(Shamt_ID), .in1({32{1'b0}}), .out(multiplexer_18_out), .sel(stall));
  Register #(.width(2)) register_11 (.D(multiplexer_10_out), .en(1'b1), .Q(ALU_Y_EX_t), .clk(clk), .clr(1'b0));
  Register #(.width(2)) register_12 (.D(multiplexer_11_out), .en(1'b1), .Q(rfw_EX), .clk(clk), .clr(1'b0));
  Register #(.width(6)) register_13 (.D(multiplexer_12_out), .en(1'b1), .Q(Jump_EX), .clk(clk), .clr(1'b0));
  Register #(.width(1)) register_14 (.D(multiplexer_13_out), .en(1'b1), .Q(rf_we_EX), .clk(clk), .clr(1'b0));
  Register #(.width(1)) register_15 (.D(multiplexer_14_out), .en(1'b1), .Q(display_EX), .clk(clk), .clr(1'b0));
  Register #(.width(1)) register_16 (.D(multiplexer_15_out), .en(1'b1), .Q(ld_ctl_EX), .clk(clk), .clr(1'b0));
  Register #(.width(1)) register_17 (.D(multiplexer_16_out), .en(1'b1), .Q(lw_lhu_EX), .clk(clk), .clr(1'b0));
  Register #(.width(1)) register_18 (.D(multiplexer_17_out), .en(1'b1), .Q(ext_EX), .clk(clk), .clr(1'b0));
  Register #(.width(32)) register_19 (.D(multiplexer_18_out), .en(1'b1), .Q(Shamt_EX), .clk(clk), .clr(1'b0));
  Multiplexer #(.width(32), .enable("false")) multiplexer_19 (
    .in0(Z_ext_EX), .in1(Shamt_EX), .out(multiplexer_19_out), .sel(ext_EX));
  Multiplexer #(.select(2), .width(32), .enable("false")) multiplexer_20 (
    .in0(RB_EX), .in1(S_ext_EX), .in2(multiplexer_19_out), .in3({32{1'b0}}), .out(ALU_Y_EX), .sel(ALU_Y_EX_t));
endmodule

// EX / MEM
module \EX_MEM流水  (
  input  [31:0] Result_EX,
  input  clk,
  input  rst,
  input  [4:0] rW_EX,
  input  str_ctl_EX,
  input  ld_ctl_EX,
  input  EN_EX,
  input  [31:0] RB_EX,
  input  rf_we_EX,
  input  [1:0] rfw_EX,
  input  lw_lhu_EX,
  input  [31:0] PC_EX,
  output [31:0] Result_MEM,
  output [4:0] rW_MEM,
  output str_ctl_MEM,
  output ld_ctl_MEM,
  output EN_MEM,
  output [31:0] RB_MEM,
  output rf_we_MEM,
  output [1:0] rfw_MEM,
  output lw_lhu_MEM,
  output [31:0] PC_MEM
);

  Register #(.width(32)) register_1 (.D(Result_EX), .en(1'b1), .Q(Result_MEM), .clk(clk), .clr(rst));
  Register #(.width(5)) register_2 (.D(rW_EX), .en(1'b1), .Q(rW_MEM), .clk(clk), .clr(rst));
  Register #(.width(1)) register_3 (.D(str_ctl_EX), .en(1'b1), .Q(str_ctl_MEM), .clk(clk), .clr(rst));
  Register #(.width(1)) register_4 (.D(ld_ctl_EX), .en(1'b1), .Q(ld_ctl_MEM), .clk(clk), .clr(rst));
  Register #(.width(1)) register_5 (.D(EN_EX), .en(1'b1), .Q(EN_MEM), .clk(clk), .clr(rst));
  Register #(.width(32)) register_6 (.D(RB_EX), .en(1'b1), .Q(RB_MEM), .clk(clk), .clr(rst));
  Register #(.width(1)) register_7 (.D(rf_we_EX), .en(1'b1), .Q(rf_we_MEM), .clk(clk), .clr(rst));
  Register #(.width(2)) register_8 (.D(rfw_EX), .en(1'b1), .Q(rfw_MEM), .clk(clk), .clr(rst));
  Register #(.width(1)) register_9 (.D(lw_lhu_EX), .en(1'b1), .Q(lw_lhu_MEM), .clk(clk), .clr(rst));
  Register #(.width(32)) register_10 (.D(PC_EX), .en(1'b1), .Q(PC_MEM), .clk(clk), .clr(rst));
endmodule

// MEM / WB
module \MEM_WB流水  (
  input  [31:0] Result_MEM,
  input  clk,
  input  rst,
  input  [4:0] rW_MEM,
  input  rf_we_MEM,
  input  EN_MEM,
  input  [31:0] MemData_MEM,
  input  [31:0] PC_MEM,
  input  lw_lhu_MEM,
  input  [1:0] rfw_MEM,
  output [4:0] rW_WB,
  output rf_we_WB,
  output EN_WB,
  output [31:0] W_MEM
);

  wire lw_lhu;
  wire [1:0] rfw;
  wire [15:0] multiplexer_1_out;
  wire [31:0] adder_1_out, bit_extender_1_out, MemData_WB, multiplexer_2_out, PC_WB, Result_WB;

  Register #(.width(32)) register_1 (.D(Result_MEM), .en(1'b1), .Q(Result_WB), .clk(clk), .clr(rst));
  Register #(.width(5)) register_2 (.D(rW_MEM), .en(1'b1), .Q(rW_WB), .clk(clk), .clr(rst));
  Register #(.width(1)) register_3 (.D(rf_we_MEM), .en(1'b1), .Q(rf_we_WB), .clk(clk), .clr(rst));
  Register #(.width(1)) register_4 (.D(EN_MEM), .en(1'b1), .Q(EN_WB), .clk(clk), .clr(rst));
  Register #(.width(32)) register_5 (.D(MemData_MEM), .en(1'b1), .Q(MemData_WB), .clk(clk), .clr(rst));
  Register #(.width(32)) register_6 (.D(PC_MEM), .en(1'b1), .Q(PC_WB), .clk(clk), .clr(rst));
  Register #(.width(1)) register_7 (.D(lw_lhu_MEM), .en(1'b1), .Q(lw_lhu), .clk(clk), .clr(rst));
  Register #(.width(2)) register_8 (.D(rfw_MEM), .en(1'b1), .Q(rfw), .clk(clk), .clr(rst));
  Multiplexer #(.width(16), .enable("false")) multiplexer_1 (
    .in0(MemData_WB[31:16]), .in1(MemData_WB[15:0]), .out(multiplexer_1_out), .sel(Result_WB[2]));
  Multiplexer #(.width(32), .enable("false")) multiplexer_2 (
    .in0(MemData_WB), .in1(bit_extender_1_out), .out(multiplexer_2_out), .sel(lw_lhu));
  Multiplexer #(.select(2), .width(32), .enable("false")) multiplexer_3 (
    .in0(Result_WB), .in1(multiplexer_2_out), .in2(adder_1_out), .out(W_MEM), .sel(rfw));  // open: in3
  assign bit_extender_1_out = {{16{multiplexer_1_out[15]}}, multiplexer_1_out};  // Bit_Extender bit_extender_1
  Adder #(.width(32)) adder_1 (.a(PC_WB), .b(32'h4), .out(adder_1_out));  // open: cin, cout
endmodule

// DECODE
module Decode (
  input  [31:0] in_1,
  output [25:0] index,
  output [31:0] S_ext,
  output [4:0] rt,
  output [31:0] Z_ext,
  output [4:0] rs,
  output [5:0] _31_26,
  output [5:0] _5_0,
  output [31:0] shamt_ext,
  output [4:0] rd
);

  assign S_ext = {{16{in_1[15]}}, in_1[15:0]};  // Bit_Extender bit_extender_1
  assign shamt_ext = {{27{1'b0}}, in_1[10:6]};  // Bit_Extender bit_extender_2
  assign Z_ext = {{16{1'b0}}, in_1[15:0]};  // Bit_Extender bit_extender_3

  assign _5_0 = in_1[5:0];
  assign _31_26 = in_1[31:26];
  assign index = in_1[25:0];
  assign rd = in_1[15:11];
  assign rs = in_1[25:21];
  assign rt = in_1[20:16];
endmodule

// CONTROL
module Control (
  input  [5:0] _31_26,
  input  [5:0] _5_0,
  input  [31:0] PCin,
  input  [31:0] v0,
  output [1:0] rfw,
  output lw_lhu,
  output rB,
  output EN,
  output ALU_X,
  output [31:0] PCout,
  output display,
  output [1:0] ALU_Y,
  output [5:0] Jump_ID,
  output rf_we,
  output [3:0] ALU_op,
  output rA,
  output str_ctl,
  output z_sh_ext,
  output [1:0] rW_ctl,
  output ld_ctl,
  output rA_on,
  output rB_on
);

  wire Add, Addi, Addiu, Addu, And, and_22_out, and_23_out, and_24_out, and_25_out, Andi, comparator_1_eq,
       Lw, Nor, nor_1_out, nor_2_out, nor_3_out, nor_4_out, not_1_out, not_2_out, not_3_out, not_4_out,
       not_5_out, not_6_out, not_7_out, not_8_out, not_9_out, not_10_out, not_11_out, not_12_out, not_13_out,
       not_14_out, not_15_out, not_16_out, not_17_out, not_18_out, Or, or_1_out, or_2_out, or_3_out,
       or_4_out, or_5_out, or_6_out, or_7_out, or_8_out, or_9_out, or_10_out, or_18_out, or_19_out, Ori, Sll,
       Slt, Slti, Sltu, Sra, Srl, Sub, Xor, Xori;

  and and_1 (Addi, ~_31_26[5], ~_31_26[4], _31_26[3], ~_31_26[2], ~_31_26[1], ~_31_26[0]);  // AND_Gate
  and and_2 (Addiu, ~_31_26[5], ~_31_26[4], _31_26[3], ~_31_26[2], ~_31_26[1], _31_26[0]);  // AND_Gate
  and and_3 (Andi, ~_31_26[5], ~_31_26[4], _31_26[3], _31_26[2], ~_31_26[1], ~_31_26[0]);  // AND_Gate
  and and_4 (Ori, ~_31_26[5], ~_31_26[4], _31_26[3], _31_26[2], ~_31_26[1], _31_26[0]);  // AND_Gate
  and and_5 (Lw, _31_26[5], ~_31_26[4], ~_31_26[3], ~_31_26[2], _31_26[1], _31_26[0]);  // AND_Gate
  and and_6 (str_ctl, _31_26[5], ~_31_26[4], _31_26[3], ~_31_26[2], _31_26[1], _31_26[0]);  // AND_Gate
  and and_7 (Jump_ID[4], ~_31_26[5], ~_31_26[4], ~_31_26[3], _31_26[2], ~_31_26[1], ~_31_26[0]);  // AND_Gate
  or or_1 (or_1_out, Add, Addu, And, Sub, Or, Xor, Nor, Jump_ID[4], Jump_ID[3], Slt, Sltu);
  or or_2 (or_2_out, Addi, Addiu, Lw, str_ctl, Slti, Xori, lw_lhu);
  or or_3 (or_3_out, Andi, Sll, Sra, Srl, Ori);
  or or_4 (or_4_out, Add, Addi, Addiu, Addu, Lw, str_ctl, lw_lhu);
  or or_5 (or_5_out, And, Andi);
  or or_6 (or_6_out, Sub, Jump_ID[0]);
  or or_7 (or_7_out, Or, Ori);
  or or_8 (or_8_out, Slt, Slti);
  or or_9 (or_9_out, Xori, Xor);
  or or_10 (or_10_out, _31_26[0], _31_26[1], _31_26[2], _31_26[3], _31_26[4], _31_26[5]);
  and and_8 (Slti, ~_31_26[5], ~_31_26[4], _31_26[3], ~_31_26[2], _31_26[1], ~_31_26[0]);  // AND_Gate
  and and_9 (Jump_ID[1], ~_31_26[5], ~_31_26[4], ~_31_26[3], ~_31_26[2], _31_26[1], ~_31_26[0]);  // AND_Gate
  and and_10 (Jump_ID[2], ~_31_26[5], ~_31_26[4], ~_31_26[3], ~_31_26[2], _31_26[1], _31_26[0]);  // AND_Gate
  and and_11 (Xori, ~_31_26[5], ~_31_26[4], _31_26[3], _31_26[2], _31_26[1], ~_31_26[0]);  // AND_Gate
  and and_12 (Jump_ID[3], ~_31_26[5], ~_31_26[4], ~_31_26[3], _31_26[2], ~_31_26[1], _31_26[0]);  // AND_Gate
  and and_13 (lw_lhu, _31_26[5], ~_31_26[4], ~_31_26[3], _31_26[2], ~_31_26[1], _31_26[0]);  // AND_Gate
  and and_14 (Jump_ID[0], ~_31_26[5], ~_31_26[4], ~_31_26[3], _31_26[2], _31_26[1], ~_31_26[0]);  // AND_Gate
  and and_15 (Add, ~or_10_out, _5_0[5], ~_5_0[4], ~_5_0[3], ~_5_0[2], ~_5_0[1], ~_5_0[0]);  // AND_Gate
  and and_16 (Addu, ~or_10_out, _5_0[5], ~_5_0[4], ~_5_0[3], ~_5_0[2], ~_5_0[1], _5_0[0]);  // AND_Gate
  and and_17 (And, ~or_10_out, _5_0[5], ~_5_0[4], ~_5_0[3], _5_0[2], ~_5_0[1], ~_5_0[0]);  // AND_Gate
  and and_18 (Sll, ~or_10_out, ~_5_0[5], ~_5_0[4], ~_5_0[3], ~_5_0[2], ~_5_0[1], ~_5_0[0]);  // AND_Gate
  and and_19 (Sra, ~or_10_out, ~_5_0[5], ~_5_0[4], ~_5_0[3], ~_5_0[2], _5_0[1], _5_0[0]);  // AND_Gate
  and and_20 (Srl, ~or_10_out, ~_5_0[5], ~_5_0[4], ~_5_0[3], ~_5_0[2], _5_0[1], ~_5_0[0]);  // AND_Gate
  and and_21 (Xor, ~or_10_out, _5_0[5], ~_5_0[4], ~_5_0[3], _5_0[2], _5_0[1], ~_5_0[0]);  // AND_Gate
  not not_1 (not_1_out, or_1_out);
  not not_2 (not_2_out, or_2_out);
  not not_3 (not_3_out, or_3_out);
  not not_4 (not_4_out, or_1_out);
  not not_5 (not_5_out, or_2_out);
  not not_6 (not_6_out, Jump_ID[0]);
  not not_7 (not_7_out, or_1_out);
  not not_8 (not_8_out, or_2_out);
  not not_9 (not_9_out, or_3_out);
  not not_10 (not_10_out, or_1_out);
  not not_11 (not_11_out, or_3_out);
  not not_12 (not_12_out, Jump_ID[0]);
  and and_22 (and_22_out, not_1_out, not_2_out, not_3_out, Jump_ID[0]);
  and and_23 (and_23_out, not_4_out, not_5_out, or_3_out, not_6_out);
  and and_24 (and_24_out, not_7_out, not_8_out, not_9_out, Jump_ID[0]);
  and and_25 (and_25_out, not_10_out, or_2_out, not_11_out, not_12_out);
  or or_11 (ALU_Y[1], and_22_out, and_23_out);
  or or_12 (ALU_Y[0], and_24_out, and_25_out);
  nor nor_1 (nor_1_out, Sll, Srl, or_6_out, or_7_out, Nor, Sltu);
  nor nor_2 (nor_2_out, or_4_out, Sll, Sra, or_7_out, Sltu, or_9_out);
  nor nor_3 (nor_3_out, Sll, Sra, Srl, or_7_out, Nor, or_8_out, or_9_out);
  nor nor_4 (nor_4_out, or_4_out, or_5_out, Sll, Sra, Srl, or_6_out);
  and and_26 (Sub, ~or_10_out, _5_0[5], ~_5_0[4], ~_5_0[3], ~_5_0[2], _5_0[1], ~_5_0[0]);  // AND_Gate
  and and_27 (Or, ~or_10_out, _5_0[5], ~_5_0[4], ~_5_0[3], _5_0[2], ~_5_0[1], _5_0[0]);  // AND_Gate
  and and_28 (Nor, ~or_10_out, _5_0[5], ~_5_0[4], ~_5_0[3], _5_0[2], _5_0[1], _5_0[0]);  // AND_Gate
  and and_29 (Slt, ~or_10_out, _5_0[5], ~_5_0[4], _5_0[3], ~_5_0[2], _5_0[1], ~_5_0[0]);  // AND_Gate
  and and_30 (Sltu, ~or_10_out, _5_0[5], ~_5_0[4], _5_0[3], ~_5_0[2], _5_0[1], _5_0[0]);  // AND_Gate
  and and_31 (Jump_ID[5], ~or_10_out, ~_5_0[5], ~_5_0[4], _5_0[3], ~_5_0[2], ~_5_0[1], ~_5_0[0]);  // AND_Gate
  and and_32 (rA, ~or_10_out, ~_5_0[5], ~_5_0[4], _5_0[3], _5_0[2], ~_5_0[1], ~_5_0[0]);  // AND_Gate
  or or_13 (ALU_op[0], or_4_out, or_5_out, Sra, or_8_out, or_9_out, nor_1_out);
  or or_14 (ALU_op[1], or_5_out, Srl, or_6_out, Nor, or_8_out, nor_2_out);
  or or_15 (ALU_op[2], or_4_out, or_5_out, or_6_out, Sltu, nor_3_out);
  or or_16 (ALU_op[3], nor_4_out, or_7_out, Nor, or_8_out, Sltu, or_9_out);
  Comparator #(.width(32)) comparator_1 (.a(v0), .b(32'ha), .eq(comparator_1_eq));  // open: gt, lt
  or or_17 (ALU_X, Sll, Sra, Srl);
  or or_18 (or_18_out, Srl, Add, Addu, And, Sll, Sra, Sub, Or, Nor, Slt, Sltu, Xor);
  or or_19 (or_19_out, Addi, Addiu, Andi, Ori, Slti, Xori, Lw, lw_lhu);
  or or_20 (ld_ctl, Lw, lw_lhu);
  nand nand_1 (EN, rA, comparator_1_eq);
  and and_33 (display, rA, ~comparator_1_eq);  // AND_Gate
  nor nor_5 (rf_we, str_ctl, Jump_ID[4], Jump_ID[3], Jump_ID[1], Jump_ID[5], rA, Jump_ID[0]);
  not not_13 (not_13_out, or_18_out);
  not not_14 (not_14_out, or_19_out);
  not not_15 (not_15_out, or_18_out);
  not not_16 (not_16_out, Jump_ID[2]);
  not not_17 (not_17_out, ld_ctl);
  not not_18 (not_18_out, Jump_ID[2]);
  and and_34 (rW_ctl[1], not_13_out, not_14_out, Jump_ID[2]);
  and and_35 (rW_ctl[0], not_15_out, or_19_out, not_16_out);
  and and_36 (rfw[1], not_17_out, Jump_ID[2]);
  and and_37 (rfw[0], ld_ctl, not_18_out);
  nor nor_6 (z_sh_ext, Andi, Ori);
  or or_21 (rA_on, Add, And, Xor, rA, Sltu, Slt, Or, Nor, Addi, Sub, Jump_ID[4], Slti, Jump_ID[3], Addu, Andi, Jump_ID[5], Ori, Addiu, Slti, str_ctl, Lw, Jump_ID[0], lw_lhu);
  or or_22 (rB_on, Sub, Xor, Add, Slt, Or, And, Nor, Srl, Sll, Sltu, Jump_ID[4], Addu, Jump_ID[3], Sra, str_ctl, rA);

  assign PCout = PCin;
  assign rB = rA;

  // Other names for the same wires on the sheet: Blez = Jump_ID[0]; J = Jump_ID[1]; Jal = Jump_ID[2];
  //   Bne = Jump_ID[3]; Beq = Jump_ID[4]; Jr = Jump_ID[5]; Lhu = lw_lhu; rW[1:0] = rW_ctl; Sw = str_ctl; syscall = rA

  // Notes on the sheet:
  //   Input
  //   Output
endmodule

module Regfile (
  input  ALU_X,
  input  [31:0] W,
  input  clk,
  input  rf_we,
  input  [4:0] rW,
  input  rA_ctl,
  input  [4:0] rs,
  input  rB_ctl,
  input  [4:0] rd,
  input  [4:0] rt,
  input  [1:0] rW_ctl,
  output [31:0] A,
  output [31:0] B,
  output [4:0] rA,
  output [4:0] rB,
  output [4:0] rW_out
);

  wire not_1_out;
  wire [31:0] registerfile_1_p7;

  not not_1 (not_1_out, clk);
  Multiplexer #(.select(2), .width(5), .enable("false")) multiplexer_1 (
    .in0(rd), .in1(rt), .in2({5{1'b1}}), .out(rW_out), .sel(rW_ctl));  // open: in3
  // RegisterFile registerfile_1: pin names not known; wires that end beside it: W, not_1_out, rf_we, rW, rA, rB, registerfile_1_p7, B
  Multiplexer #(.width(5), .enable("false")) multiplexer_2 (.in0(rs), .in1(5'b00010), .out(rA), .sel(rA_ctl));
  Multiplexer #(.width(5), .enable("false")) multiplexer_3 (.in0(rt), .in1(5'b00100), .out(rB), .sel(rB_ctl));
  Multiplexer #(.width(32), .enable("false")) multiplexer_4 (.in0(registerfile_1_p7), .in1(B), .out(A), .sel(ALU_X));

  // Notes on the sheet:
  //   寄存器文件
endmodule

module PC (
  input  [31:0] PC_new,
  input  EN,
  input  clk,
  input  rst,
  output [31:0] PC_now
);

  Register #(.width(32)) PC (.D(PC_new), .en(EN), .Q(PC_now), .clk(clk), .clr(rst));
endmodule

module NPC (
  input  [31:0] J__rs,
  input  [1:0] NPC_op,
  input  PC_Con,
  input  [15:0] B_offset,
  input  [31:0] \PC_有条件 ,
  input  [25:0] JMP_index,
  input  [31:0] PC_in,
  output [31:0] PC_new
);

  wire [31:0] adder_1_out, adder_2_out, bit_extender_1_out, multiplexer_2_out;

  assign bit_extender_1_out = {{14{B_offset[15]}}, {B_offset, 2'b00}};  // Bit_Extender bit_extender_1
  Adder #(.width(32)) adder_1 (.a(adder_2_out), .b(bit_extender_1_out), .out(adder_1_out));  // open: cin, cout
  Multiplexer #(.select(2), .width(32), .enable("false")) multiplexer_1 (
    .in0(adder_2_out), .in1({PC_in[31:28], JMP_index, 2'b00}), .in2(adder_1_out), .in3(J__rs), .out(PC_new),
    .sel(NPC_op));
  Multiplexer #(.width(32), .enable("false")) multiplexer_2 (
    .in0(PC_in), .in1(\PC_有条件 ), .out(multiplexer_2_out), .sel(PC_Con));
  Adder #(.width(32)) adder_2 (.a(32'h4), .b(multiplexer_2_out), .out(adder_2_out));  // open: cin, cout
endmodule

module Data_Conflict (
  input  [4:0] rW_EX,
  input  [4:0] rA,
  input  [4:0] rW_MEM,
  input  [4:0] rB,
  input  rf_we_EX,
  input  rf_we_MEM,
  input  rA_on,
  input  rB_on,
  input  J,
  output stall
);

  wire and_1_out, and_2_out, and_3_out, and_4_out, and_5_out, and_6_out, and_7_out, and_8_out,
       comparator_1_eq, comparator_2_eq, comparator_3_eq, comparator_4_eq, comparator_5_eq, comparator_6_eq,
       not_1_out, not_2_out, not_3_out, not_4_out, not_5_out, not_6_out;

  Comparator #(.width(5)) comparator_1 (.a({5{1'b0}}), .b(rW_EX), .eq(comparator_1_eq));  // open: gt, lt
  Comparator #(.width(5)) comparator_2 (.a(rA), .b(rW_EX), .eq(comparator_2_eq));  // open: gt, lt
  not not_1 (not_1_out, comparator_1_eq);
  Comparator #(.width(5)) comparator_3 (.a(rA), .b(rW_MEM), .eq(comparator_3_eq));  // open: gt, lt
  Comparator #(.width(5)) comparator_4 (.a(rB), .b(rW_EX), .eq(comparator_4_eq));  // open: gt, lt
  Comparator #(.width(5)) comparator_5 (.a(rB), .b(rW_MEM), .eq(comparator_5_eq));  // open: gt, lt
  not not_2 (not_2_out, comparator_6_eq);
  Comparator #(.width(5)) comparator_6 (.a({5{1'b0}}), .b(rW_MEM), .eq(comparator_6_eq));  // open: gt, lt
  and and_1 (and_1_out, comparator_2_eq, not_1_out, rf_we_EX, rA_on);
  and and_2 (and_2_out, rf_we_MEM, comparator_3_eq, not_2_out, rA_on);
  and and_3 (and_3_out, not_1_out, comparator_4_eq, rf_we_EX, rB_on);
  and and_4 (and_4_out, rf_we_MEM, comparator_5_eq, not_2_out, rB_on);
  not not_3 (not_3_out, J);
  not not_4 (not_4_out, J);
  not not_5 (not_5_out, J);
  not not_6 (not_6_out, J);
  and and_5 (and_5_out, and_1_out, not_3_out);
  and and_6 (and_6_out, and_2_out, not_4_out);
  and and_7 (and_7_out, and_3_out, not_5_out);
  and and_8 (and_8_out, and_4_out, not_6_out);
  or or_1 (stall, and_5_out, and_6_out, and_7_out, and_8_out);
endmodule

module Ctl_Conflict (
  input  [5:0] Jump_EX,
  input  eql,
  input  [31:0] Result,
  output [1:0] NPC_op,
  output Jump,
  output Con,
  output Condit_Sec,
  output Uncondit,
  output Condit
);

  wire _0, and_1_out, and_2_out, and_3_out, and_4_out, and_5_out, and_6_out, and_7_out, and_8_out, and_9_out,
       and_10_out, and_11_out, and_12_out, and_13_out, and_14_out, comparator_1_eq, comparator_1_lt,
       not_1_out, not_2_out, not_3_out, not_4_out, not_5_out, not_6_out, not_7_out, not_8_out, not_9_out,
       not_10_out, not_11_out, not_12_out, or_1_out, or_2_out, or_3_out, or_4_out;

  not not_1 (not_1_out, eql);
  and and_1 (and_1_out, Jump_EX[4], eql);
  and and_2 (and_2_out, Jump_EX[3], not_1_out);
  and and_3 (and_3_out, Jump_EX[0], _0);
  or or_1 (or_1_out, Jump_EX[1], Jump_EX[2]);
  not not_2 (not_2_out, eql);
  or or_2 (or_2_out, and_1_out, and_2_out, and_3_out);
  and and_4 (and_4_out, Jump_EX[4], eql);
  and and_5 (and_5_out, Jump_EX[3], not_2_out);
  or or_3 (or_3_out, and_4_out, and_5_out, and_6_out);
  and and_6 (and_6_out, Jump_EX[0], _0);
  or or_4 (or_4_out, Jump_EX[1], Jump_EX[5]);
  not not_3 (not_3_out, or_1_out);
  not not_4 (not_4_out, or_2_out);
  not not_5 (not_5_out, or_1_out);
  not not_6 (not_6_out, Jump_EX[5]);
  not not_7 (not_7_out, or_1_out);
  not not_8 (not_8_out, or_2_out);
  not not_9 (not_9_out, or_2_out);
  not not_10 (not_10_out, Jump_EX[5]);
  and and_7 (and_7_out, not_3_out, not_4_out, Jump_EX[5]);
  or or_5 (NPC_op[1], and_7_out, and_8_out);
  and and_8 (and_8_out, not_5_out, or_2_out, not_6_out);
  and and_9 (and_9_out, not_7_out, not_8_out, Jump_EX[5]);
  or or_6 (NPC_op[0], and_9_out, and_10_out);
  and and_10 (and_10_out, or_1_out, not_9_out, not_10_out);
  // OR_Gate or_7 has open pins: in0=or_3_out, in1=or_4_out, out=open
  or or_8 (Uncondit, Jump_EX[1], Jump_EX[2], Jump_EX[5]);
  or or_9 (Condit, Jump_EX[4], Jump_EX[0], Jump_EX[3]);
  and and_11 (and_11_out, Jump_EX[4], eql);
  not not_11 (not_11_out, eql);
  not not_12 (not_12_out, eql);
  and and_12 (and_12_out, not_11_out, Jump_EX[3]);
  and and_13 (and_13_out, Jump_EX[4], eql);
  and and_14 (and_14_out, not_12_out, Jump_EX[3]);
  and and_15 (Condit_Sec, ~NPC_op[0], NPC_op[1]);  // AND_Gate
  Comparator #(.width(32)) comparator_1 (
    .a(Result), .b({32{1'b0}}), .eq(comparator_1_eq), .lt(comparator_1_lt));  // open: gt
  or or_10 (Jump, and_11_out, and_12_out, Jump_EX[1], Jump_EX[2], Jump_EX[5]);
  or or_11 (Con, and_13_out, and_14_out);
  or or_12 (_0, comparator_1_eq, comparator_1_lt);

  // Other names for the same wires on the sheet: Blez = Jump_EX[0]; J = Jump_EX[1]; Jal = Jump_EX[2];
  //   Bne = Jump_EX[3]; Beq = Jump_EX[4]; Jr = Jump_EX[5]
endmodule
