// Logisim project cpu_理想 .circ as structural Verilog: 7 circuits, main circuit cpu
module cpu (
);

  wire clock_1_out, control_1_ra, control_1_rb, control_1_rf_we, control_1_str_ctl, EN, EN_MEM,
       ex_mem_1_en_mem, ex_mem_1_rf_we_mem, ex_mem_1_str_ctl_mem, id_ex_1_en_ex, id_ex_1_rf_we_ex,
       id_ex_1_str_ctl_ex, not_1_out, not_2_out, register_1_q, rf_we, RST;
  wire [1:0] control_1_alu_y, control_1_rw, ex_mem_1_rw_mem, id_ex_1_alu_y_ex, id_ex_1_rw_ex, rW;
  wire [3:0] control_1_alu_op, id_ex_1_alu_op_ex;
  wire [4:0] ex_mem_1_rt_mem, id_ex_1_rt_ex, multiplexer_1_out, multiplexer_2_out, rd, rs, rt, rt_WB;
  wire [5:0] decode_1__5_0, decode_1__31_26;
  wire [15:0] \总周期数 , \无条件分支指令数 , \有条件分支成功跳转 , \有条件分支指令数 ;
  wire [31:0] adder_1_out, alu_1_result, ex_mem_1_rb_mem, ex_mem_1_result_mem, id_ex_1_r2_ex, id_ex_1_ra_ex,
       id_ex_1_s_ext_ex, id_ex_1_z_ext_ex, if_id_1_idin, multiplexer_3_out, PC_q, registerfile_1_p8,
       rom_1_data, S_ext, SyscallOut, v0, W, Z_ext;

  Button \u_总复位  (.out(RST));
  Clock clock_1 (.out(clock_1_out));
  Register #(.width(32)) PC (.D(adder_1_out), .en(not_2_out), .Q(PC_q), .clk(clock_1_out), .clr(RST));
  Hex_Digit_Display hex_digit_display_1 (.value(SyscallOut[27:24]));  // open: dp
  Hex_Digit_Display hex_digit_display_2 (.value(SyscallOut[31:28]));  // open: dp
  Adder #(.width(32)) adder_1 (.a(32'h4), .b(PC_q), .out(adder_1_out));  // open: cin, cout
  Hex_Digit_Display hex_digit_display_3 (.value(SyscallOut[23:20]));  // open: dp
  Hex_Digit_Display hex_digit_display_4 (.value(SyscallOut[19:16]));  // open: dp
  Hex_Digit_Display hex_digit_display_5 (.value(SyscallOut[11:8]));  // open: dp
  Hex_Digit_Display hex_digit_display_6 (.value(SyscallOut[15:12]));  // open: dp
  IF_ID if_id_1 (
    .IFin(rom_1_data), .clk(clock_1_out), .PC_4_IF(PC_q), .IDin(if_id_1_idin), .RST(RST));  // open: PC_4_ID
  ROM #(.addrWidth(10), .dataWidth(32)) rom_1 (.addr(PC_q[11:2]), .data(rom_1_data));  // open: sel
  Hex_Digit_Display hex_digit_display_7 (.value(SyscallOut[3:0]));  // open: dp
  Hex_Digit_Display hex_digit_display_8 (.value(SyscallOut[7:4]));  // open: dp
  Decode decode_1 (
    .in_1(if_id_1_idin), .S_ext(S_ext), .Z_ext(Z_ext), ._5_0(decode_1__5_0), ._31_26(decode_1__31_26),
    .rs(rs), .rt(rt), .rd(rd));  // open: index
  Control control_1 (
    ._31_26(decode_1__31_26), ._5_0(decode_1__5_0), .v0(v0), .rB(control_1_rb), .EN(EN),
    .ALU_Y(control_1_alu_y), .rf_we(control_1_rf_we), .ALU_op(control_1_alu_op), .rA(control_1_ra),
    .str_ctl(control_1_str_ctl), .rW(control_1_rw));  // open: ALU_X, lw_lhu
  // Probe on \总周期数 
  // Probe on \无条件分支指令数 
  // Probe on \有条件分支指令数 
  // Probe on \有条件分支成功跳转 
  Multiplexer #(.width(5), .enable("false")) multiplexer_1 (
    .in0(rs), .in1(5'b00010), .out(multiplexer_1_out), .sel(control_1_ra));
  Multiplexer #(.width(5), .enable("false")) multiplexer_2 (
    .in0(rt), .in1(5'b00100), .out(multiplexer_2_out), .sel(control_1_rb));
  // RegisterFile registerfile_1: pin names not known; wires that end beside it: W, clock_1_out, rf_we, rt_WB, multiplexer_1_out, multiplexer_2_out, v0, registerfile_1_p8
  not not_1 (not_1_out, EN);
  ID_EX id_ex_1 (
    .S_ext_ID(S_ext), .clk(clock_1_out), .RA_ID(v0), .rf_we_ID(control_1_rf_we), .RB_ID(registerfile_1_p8),
    .rW_ID(control_1_rw), .ALU_op_ID(control_1_alu_op), .str_ctl_ID(control_1_str_ctl), .EN_ID(not_1_out),
    .S_ext_EX(id_ex_1_s_ext_ex), .RA_EX(id_ex_1_ra_ex), .rf_we_EX(id_ex_1_rf_we_ex), .R2_EX(id_ex_1_r2_ex),
    .rW_EX(id_ex_1_rw_ex), .ALU_op_EX(id_ex_1_alu_op_ex), .str_ctl_EX(id_ex_1_str_ctl_ex),
    .EN_EX(id_ex_1_en_ex), .rst(RST), .ALU_Y_EX(id_ex_1_alu_y_ex), .ALU_Y_ID(control_1_alu_y),
    .Z_ext_ID(Z_ext), .Z_ext_EX(id_ex_1_z_ext_ex), .rt_ID(rt), .rt_EX(id_ex_1_rt_ex));  // open: ALU_X_EX, ALU_X_ID
  // Probe on id_ex_1_en_ex
  ALU alu_1 (
    .AluOP(id_ex_1_alu_op_ex), .X(id_ex_1_ra_ex), .Result(alu_1_result), .Y(multiplexer_3_out));  // open: Equal, Signed_Overflow, Result_2, UnSigned_Overflow, out_9
  Multiplexer #(.select(2), .width(32), .enable("false")) multiplexer_3 (
    .in0(id_ex_1_r2_ex), .in1(id_ex_1_s_ext_ex), .in2(id_ex_1_z_ext_ex), .out(multiplexer_3_out),
    .sel(id_ex_1_alu_y_ex));  // open: in3
  EX_MEM ex_mem_1 (
    .Result_EX(alu_1_result), .rt_EX(id_ex_1_rt_ex), .Result_MEM(ex_mem_1_result_mem), .rst(RST),
    .rt_MEM(ex_mem_1_rt_mem), .clk(clock_1_out), .str_ctl_EX(id_ex_1_str_ctl_ex),
    .str_ctl_MEM(ex_mem_1_str_ctl_mem), .rW_EX(id_ex_1_rw_ex), .rW_MEM(ex_mem_1_rw_mem),
    .EN_EX(id_ex_1_en_ex), .EN_MEM(ex_mem_1_en_mem), .RB_EX(id_ex_1_r2_ex), .RB_MEM(ex_mem_1_rb_mem),
    .rf_we_EX(id_ex_1_rf_we_ex), .rf_we_MEM(ex_mem_1_rf_we_mem));
  // Probe on ex_mem_1_en_mem
  // Probe on \总周期数 
  // MIPS_RAM mips_ram_1: pin names not known; wires that end beside it: ex_mem_1_rb_mem, ex_mem_1_str_ctl_mem, clock_1_out, RST
  MEM_WB mem_wb_1 (
    .Result_MEM(ex_mem_1_result_mem), .clk(clock_1_out), .rW_EX(ex_mem_1_rw_mem), .EN_EX(ex_mem_1_en_mem),
    .Result_WB(W), .rst(RST), .rW_MEM(rW), .EN_MEM(EN_MEM), .rf_we_EX(ex_mem_1_rf_we_mem), .rf_we_MEM(rf_we),
    .rt_MEM(ex_mem_1_rt_mem), .rt_WB(rt_WB));  // open: rt_EX, rt_MEM_2
  // Probe on EN_MEM
  Register #(.width(1)) register_1 (.D(EN_MEM), .en(EN_MEM), .Q(register_1_q), .clk(clock_1_out), .clr(RST));
  not not_2 (not_2_out, register_1_q);
  // Probe on \总周期数 
  Counter #(.width(16), .max('hffff)) counter_1 (
    .load(1'b0), .count(not_2_out), .Q(\总周期数 ), .clk(clock_1_out), .clr(RST));  // open: D, carry

  // Notes on the sheet:
  //   数码管输出应该用寄存器锁存，否则显示数据只能一闪而过
  //   可以通过项目增加Logisim库的方式将前几次实验完成的电路作为子电路引入到本电路中使用
  //   指令存储器
  //   contents of rom_1 (hex, n*v repeats v):
  //   20100000 20110000 20120000 20130000 36100000 36310001 36520002 36730003 ae100000 ae110004 ae120008
  //   ae13000c 2002000a 20110000 20120000 20130000 c
  //   数码管输出
  //   总复位信号应将除ROM以外所有存储组件全部清零
  //   寄存器文件
endmodule

module IF_ID (
  input  [31:0] IFin,
  input  clk,
  input  [31:0] PC_4_IF,
  input  RST,
  output [31:0] IDin,
  output [31:0] PC_4_ID
);

  Register #(.width(32)) register_1 (.D(IFin), .en(1'b1), .Q(IDin), .clk(clk), .clr(RST));
  Register #(.width(32)) register_2 (.D(PC_4_IF), .en(1'b1), .Q(PC_4_ID), .clk(clk), .clr(RST));
endmodule

module ID_EX (
  input  [31:0] S_ext_ID,
  input  clk,
  input  rst,
  input  [31:0] RA_ID,
  input  [31:0] RB_ID,
  input  [1:0] ALU_Y_ID,
  input  ALU_X_ID,
  input  [31:0] Z_ext_ID,
  input  EN_ID,
  input  [3:0] ALU_op_ID,
  input  rf_we_ID,
  input  str_ctl_ID,
  input  [1:0] rW_ID,
  input  [4:0] rt_ID,
  output [31:0] S_ext_EX,
  output [31:0] RA_EX,
  output [31:0] R2_EX,
  output [1:0] ALU_Y_EX,
  output ALU_X_EX,
  output [31:0] Z_ext_EX,
  output EN_EX,
  output [3:0] ALU_op_EX,
  output rf_we_EX,
  output str_ctl_EX,
  output [1:0] rW_EX,
  output [4:0] rt_EX
);

  Register #(.width(32)) register_1 (.D(S_ext_ID), .en(1'b1), .Q(S_ext_EX), .clk(clk), .clr(rst));
  Register #(.width(32)) register_2 (.D(RA_ID), .en(1'b1), .Q(RA_EX), .clk(clk), .clr(rst));
  Register #(.width(32)) register_3 (.D(RB_ID), .en(1'b1), .Q(R2_EX), .clk(clk), .clr(rst));
  Register #(.width(32)) register_4 (.D(Z_ext_ID), .en(1'b1), .Q(Z_ext_EX), .clk(clk), .clr(rst));
  Register #(.width(4)) register_5 (.D(ALU_op_ID), .en(1'b1), .Q(ALU_op_EX), .clk(clk), .clr(rst));
  Register #(.width(1)) register_6 (.D(str_ctl_ID), .en(1'b1), .Q(str_ctl_EX), .clk(clk), .clr(rst));
  Register #(.width(5)) register_7 (.D(rt_ID), .en(1'b1), .Q(rt_EX), .clk(clk), .clr(rst));
  Register #(.width(2)) register_8 (.D(ALU_Y_ID), .en(1'b1), .Q(ALU_Y_EX), .clk(clk), .clr(rst));
  Register #(.width(1)) register_9 (.D(ALU_X_ID), .en(1'b1), .Q(ALU_X_EX), .clk(clk), .clr(rst));
  Register #(.width(1)) register_10 (.D(EN_ID), .en(1'b1), .Q(EN_EX), .clk(clk), .clr(rst));
  Register #(.width(1)) register_11 (.D(rf_we_ID), .en(1'b1), .Q(rf_we_EX), .clk(clk), .clr(rst));
  Register #(.width(2)) register_12 (.D(rW_ID), .en(1'b1), .Q(rW_EX), .clk(clk), .clr(rst));
endmodule

// EX / MEM
module EX_MEM (
  input  [31:0] Result_EX,
  input  clk,
  input  rst,
  input  [4:0] rt_EX,
  input  str_ctl_EX,
  input  [1:0] rW_EX,
  input  EN_EX,
  input  [31:0] RB_EX,
  input  rf_we_EX,
  output [31:0] Result_MEM,
  output [4:0] rt_MEM,
  output str_ctl_MEM,
  output [1:0] rW_MEM,
  output EN_MEM,
  output [31:0] RB_MEM,
  output rf_we_MEM
);

  Register #(.width(32)) register_1 (.D(Result_EX), .en(1'b1), .Q(Result_MEM), .clk(clk), .clr(rst));
  Register #(.width(5)) register_2 (.D(rt_EX), .en(1'b1), .Q(rt_MEM), .clk(clk), .clr(rst));
  Register #(.width(1)) register_3 (.D(str_ctl_EX), .en(1'b1), .Q(str_ctl_MEM), .clk(clk), .clr(rst));
  Register #(.width(2)) register_4 (.D(rW_EX), .en(1'b1), .Q(rW_MEM), .clk(clk), .clr(rst));
  Register #(.width(1)) register_5 (.D(EN_EX), .en(1'b1), .Q(EN_MEM), .clk(clk), .clr(rst));
  Register #(.width(32)) register_6 (.D(RB_EX), .en(1'b1), .Q(RB_MEM), .clk(clk), .clr(rst));
  Register #(.width(1)) register_7 (.D(rf_we_EX), .en(1'b1), .Q(rf_we_MEM), .clk(clk), .clr(rst));
endmodule

// MEM / WB
module MEM_WB (
  input  [31:0] Result_MEM,
  input  clk,
  input  rst,
  input  [4:0] rt_EX,
  input  rf_we_EX,
  input  [1:0] rW_EX,
  input  EN_EX,
  input  [4:0] rt_MEM,
  output [31:0] Result_WB,
  output [4:0] rt_MEM_2,
  output rf_we_MEM,
  output [1:0] rW_MEM,
  output EN_MEM,
  output [4:0] rt_WB
);

  Register #(.width(32)) register_1 (.D(Result_MEM), .en(1'b1), .Q(Result_WB), .clk(clk), .clr(rst));
  Register #(.width(5)) register_2 (.D(rt_EX), .en(1'b1), .Q(rt_MEM_2), .clk(clk), .clr(rst));
  Register #(.width(1)) register_3 (.D(rf_we_EX), .en(1'b1), .Q(rf_we_MEM), .clk(clk), .clr(rst));
  Register #(.width(2)) register_4 (.D(rW_EX), .en(1'b1), .Q(rW_MEM), .clk(clk), .clr(rst));
  Register #(.width(1)) register_5 (.D(EN_EX), .en(1'b1), .Q(EN_MEM), .clk(clk), .clr(rst));
  Register #(.width(5)) register_6 (.D(rt_MEM), .en(1'b1), .Q(rt_WB), .clk(clk), .clr(rst));
endmodule

// DECODE
module Decode (
  input  [31:0] in_1,
  output [25:0] index,
  output [31:0] S_ext,
  output [4:0] rt,
  output [31:0] Z_ext,
  output [4:0] rs,
  output [5:0] _31_26,
  output [5:0] _5_0,
  output [4:0] rd
);

  assign S_ext = {{16{in_1[15]}}, in_1[15:0]};  // Bit_Extender bit_extender_1
  assign Z_ext = {{16{1'b0}}, in_1[15:0]};  // Bit_Extender bit_extender_2

  assign _5_0 = in_1[5:0];
  assign _31_26 = in_1[31:26];
  assign index = in_1[25:0];
  assign rd = in_1[15:11];
  assign rs = in_1[25:21];
  assign rt = in_1[20:16];
endmodule

// CONTROL
module Control (
  input  [5:0] _31_26,
  input  [5:0] _5_0,
  input  [31:0] v0,
  output rB,
  output EN,
  output ALU_X,
  output [1:0] ALU_Y,
  output lw_lhu,
  output rf_we,
  output [3:0] ALU_op,
  output rA,
  output str_ctl,
  output [1:0] rW
);

  wire Add, Addi, Addiu, Addu, And, and_22_out, and_23_out, and_24_out, and_25_out, Andi, Beq, Blez, Bne,
       comparator_1_eq, J, Jal, Jr, Lw, Nor, nor_1_out, nor_2_out, nor_3_out, nor_4_out, not_1_out,
       not_2_out, not_3_out, not_4_out, not_5_out, not_6_out, not_7_out, not_8_out, not_9_out, not_10_out,
       not_11_out, not_12_out, not_13_out, not_14_out, not_15_out, not_16_out, Or, or_1_out, or_2_out,
       or_3_out, or_4_out, or_5_out, or_6_out, or_7_out, or_8_out, or_9_out, or_10_out, or_18_out, or_19_out,
       Ori, Sll, Slt, Slti, Sltu, Sra, Srl, Sub, Xor, Xori;

  and and_1 (Addi, ~_31_26[5], ~_31_26[4], _31_26[3], ~_31_26[2], ~_31_26[1], ~_31_26[0]);  // AND_Gate
  and and_2 (Addiu, ~_31_26[5], ~_31_26[4], _31_26[3], ~_31_26[2], ~_31_26[1], _31_26[0]);  // AND_Gate
  and and_3 (Andi, ~_31_26[5], ~_31_26[4], _31_26[3], _31_26[2], ~_31_26[1], ~_31_26[0]);  // AND_Gate
  and and_4 (Ori, ~_31_26[5], ~_31_26[4], _31_26[3], _31_26[2], ~_31_26[1], _31_26[0]);  // AND_Gate
  and and_5 (Lw, _31_26[5], ~_31_26[4], ~_31_26[3], ~_31_26[2], _31_26[1], _31_26[0]);  // AND_Gate
  and and_6 (str_ctl, _31_26[5], ~_31_26[4], _31_26[3], ~_31_26[2], _31_26[1], _31_26[0]);  // AND_Gate
  and and_7 (Beq, ~_31_26[5], ~_31_26[4], ~_31_26[3], _31_26[2], ~_31_26[1], ~_31_26[0]);  // AND_Gate
  or or_1 (or_1_out, Add, Addu, And, Sub, Or, Xor, Nor, Beq, Bne, Slt, Sltu);
  or or_2 (or_2_out, Addi, Addiu, Lw, str_ctl, Slti, Xori, lw_lhu);
  or or_3 (or_3_out, Andi, Sll, Sra, Srl, Ori);
  or or_4 (or_4_out, Add, Addi, Addiu, Addu, Lw, str_ctl, lw_lhu);
  or or_5 (or_5_out, And, Andi);
  or or_6 (or_6_out, Sub, Blez);
  or or_7 (or_7_out, Or, Ori);
  or or_8 (or_8_out, Slt, Slti);
  or or_9 (or_9_out, Xori, Xor);
  or or_10 (or_10_out, _31_26[0], _31_26[1], _31_26[2], _31_26[3], _31_26[4], _31_26[5]);
  and and_8 (Slti, ~_31_26[5], ~_31_26[4], _31_26[3], ~_31_26[2], _31_26[1], ~_31_26[0]);  // AND_Gate
  and and_9 (J, ~_31_26[5], ~_31_26[4], ~_31_26[3], ~_31_26[2], _31_26[1], ~_31_26[0]);  // AND_Gate
  and and_10 (Jal, ~_31_26[5], ~_31_26[4], ~_31_26[3], ~_31_26[2], _31_26[1], _31_26[0]);  // AND_Gate
  and and_11 (Xori, ~_31_26[5], ~_31_26[4], _31_26[3], _31_26[2], _31_26[1], ~_31_26[0]);  // AND_Gate
  and and_12 (Bne, ~_31_26[5], ~_31_26[4], ~_31_26[3], _31_26[2], ~_31_26[1], _31_26[0]);  // AND_Gate
  and and_13 (lw_lhu, _31_26[5], ~_31_26[4], ~_31_26[3], _31_26[2], ~_31_26[1], _31_26[0]);  // AND_Gate
  and and_14 (Blez, ~_31_26[5], ~_31_26[4], ~_31_26[3], _31_26[2], _31_26[1], ~_31_26[0]);  // AND_Gate
  and and_15 (Add, ~or_10_out, _5_0[5], ~_5_0[4], ~_5_0[3], ~_5_0[2], ~_5_0[1], ~_5_0[0]);  // AND_Gate
  and and_16 (Addu, ~or_10_out, _5_0[5], ~_5_0[4], ~_5_0[3], ~_5_0[2], ~_5_0[1], _5_0[0]);  // AND_Gate
  and and_17 (And, ~or_10_out, _5_0[5], ~_5_0[4], ~_5_0[3], _5_0[2], ~_5_0[1], ~_5_0[0]);  // AND_Gate
  and and_18 (Sll, ~or_10_out, ~_5_0[5], ~_5_0[4], ~_5_0[3], ~_5_0[2], ~_5_0[1], ~_5_0[0]);  // AND_Gate
  and and_19 (Sra, ~or_10_out, ~_5_0[5], ~_5_0[4], ~_5_0[3], ~_5_0[2], _5_0[1], _5_0[0]);  // AND_Gate
  and and_20 (Srl, ~or_10_out, ~_5_0[5], ~_5_0[4], ~_5_0[3], ~_5_0[2], _5_0[1], ~_5_0[0]);  // AND_Gate
  and and_21 (Xor, ~or_10_out, _5_0[5], ~_5_0[4], ~_5_0[3], _5_0[2], _5_0[1], ~_5_0[0]);  // AND_Gate
  not not_1 (not_1_out, or_1_out);
  not not_2 (not_2_out, or_2_out);
  not not_3 (not_3_out, or_3_out);
  not not_4 (not_4_out, or_1_out);
  not not_5 (not_5_out, or_2_out);
  not not_6 (not_6_out, Blez);
  not not_7 (not_7_out, or_1_out);
  not not_8 (not_8_out, or_2_out);
  not not_9 (not_9_out, or_3_out);
  not not_10 (not_10_out, or_1_out);
  not not_11 (not_11_out, or_3_out);
  not not_12 (not_12_out, Blez);
  and and_22 (and_22_out, not_1_out, not_2_out, not_3_out, Blez);
  and and_23 (and_23_out, not_4_out, not_5_out, or_3_out, not_6_out);
  and and_24 (and_24_out, not_7_out, not_8_out, not_9_out, Blez);
  and and_25 (and_25_out, not_10_out, or_2_out, not_11_out, not_12_out);
  or or_11 (ALU_Y[1], and_22_out, and_23_out);
  or or_12 (ALU_Y[0], and_24_out, and_25_out);
  nor nor_1 (nor_1_out, Sll, Srl, or_6_out, or_7_out, Nor, Sltu);
  nor nor_2 (nor_2_out, or_4_out, Sll, Sra, or_7_out, Sltu, or_9_out);
  nor nor_3 (nor_3_out, Sll, Sra, Srl, or_7_out, Nor, or_8_out, or_9_out);
  nor nor_4 (nor_4_out, or_4_out, or_5_out, Sll, Sra, Srl, or_6_out);
  and and_26 (Sub, ~or_10_out, _5_0[5], ~_5_0[4], ~_5_0[3], ~_5_0[2], _5_0[1], ~_5_0[0]);  // AND_Gate
  and and_27 (Or, ~or_10_out, _5_0[5], ~_5_0[4], ~_5_0[3], _5_0[2], ~_5_0[1], _5_0[0]);  // AND_Gate
  and and_28 (Nor, ~or_10_out, _5_0[5], ~_5_0[4], ~_5_0[3], _5_0[2], _5_0[1], _5_0[0]);  // AND_Gate
  and and_29 (Slt, ~or_10_out, _5_0[5], ~_5_0[4], _5_0[3], ~_5_0[2], _5_0[1], ~_5_0[0]);  // AND_Gate
  and and_30 (Sltu, ~or_10_out, _5_0[5], ~_5_0[4], _5_0[3], ~_5_0[2], _5_0[1], _5_0[0]);  // AND_Gate
  and and_31 (Jr, ~or_10_out, ~_5_0[5], ~_5_0[4], _5_0[3], ~_5_0[2], ~_5_0[1], ~_5_0[0]);  // AND_Gate
  and and_32 (rA, ~or_10_out, ~_5_0[5], ~_5_0[4], _5_0[3], _5_0[2], ~_5_0[1], ~_5_0[0]);  // AND_Gate
  or or_13 (ALU_op[0], or_4_out, or_5_out, Sra, or_8_out, or_9_out, nor_1_out);
  or or_14 (ALU_op[1], or_5_out, Srl, or_6_out, Nor, or_8_out, nor_2_out);
  or or_15 (ALU_op[2], or_4_out, or_5_out, or_6_out, Sltu, nor_3_out);
  or or_16 (ALU_op[3], nor_4_out, or_7_out, Nor, or_8_out, Sltu, or_9_out);
  Comparator #(.width(32)) comparator_1 (.a(v0), .b(32'ha), .eq(comparator_1_eq));  // open: gt, lt
  or or_17 (ALU_X, Sll, Sra, Srl);
  or or_18 (or_18_out, Srl, Add, Addu, And, Sll, Sra, Sub, Or, Nor, Slt, Sltu, Xor);
  or or_19 (or_19_out, Addi, Addiu, Andi, Ori, Slti, Xori, Lw, lw_lhu);
  nand nand_1 (EN, rA, comparator_1_eq);
  nor nor_5 (rf_we, str_ctl, Beq, Bne, J, Jr, rA, Blez);
  not not_13 (not_13_out, or_18_out);
  not not_14 (not_14_out, or_19_out);
  not not_15 (not_15_out, or_18_out);
  not not_16 (not_16_out, Jal);
  and and_33 (rW[1], not_13_out, not_14_out, Jal);
  and and_34 (rW[0], not_15_out, or_19_out, not_16_out);

  assign rB = rA;

  // Other names for the same wires on the sheet: Lhu = lw_lhu; Sw = str_ctl; syscall = rA

  // Notes on the sheet:
  //   Input
  //   Output
endmodule
